// Logisim project teamwork.circ as structural Verilog
module \游戏面板  (
);

  wire and_1_out, CLK, comparator_1_eq, comparator_1_lt, or_1_out, RST, START, \减速 , \加速 ;
  wire [3:0] \HP个位 , \HP十位 , \HP百位 ;
  wire [15:0] \速度 , \速度初始 ;

  DotMatrix #(.inputtype("column"), .matrixcols(9), .matrixrows(9), .persist(0), .dotshape("square")) dotmatrix_1 (
    .col0({9{1'b0}}), .col1(9'h78), .col2(9'hfc), .col3(9'hfe), .col4(9'h7f), .col5(9'hfe), .col6(9'hfc),
    .col7(9'h78), .col8({9{1'b0}}));
  Hex_Digit_Display hex_digit_display_1 (.value(\HP百位 ));  // open: dp
  Hex_Digit_Display hex_digit_display_2 (.value(\HP个位 ));  // open: dp
  Hex_Digit_Display hex_digit_display_3 (.value(\HP十位 ));  // open: dp
  Button button_1 (.out(START));
  Button button_2 (.out(RST));
  Clock #(.highDuration(1), .lowDuration(1)) clock_1 (.out(CLK));
  Button button_3 (.out(\加速 ));
  Button button_4 (.out(\减速 ));
  DotMatrix #(.inputtype("row"), .matrixcols(32), .matrixrows(32), .persist(0), .dotshape("square")) dotmatrix_2 ();  // open: row0, row1, row2, row3, row4, row5, row6, row7, row8, row9, row10, row11, row12, row13, row14, row15, row16, row17, row18, row19, row20, row21, row22, row23, row24, row25, row26, row27, row28, row29, row30, row31
  DotMatrix #(.inputtype("row"), .matrixcols(32), .matrixrows(32), .persist(0), .dotshape("square")) dotmatrix_3 ();  // open: row0, row1, row2, row3, row4, row5, row6, row7, row8, row9, row10, row11, row12, row13, row14, row15, row16, row17, row18, row19, row20, row21, row22, row23, row24, row25, row26, row27, row28, row29, row30, row31
  Comparator #(.width(16), .mode("twosComplement")) comparator_1 (
    .a(\速度初始 ), .b(16'h1), .eq(comparator_1_eq), .lt(comparator_1_lt));  // open: gt
  Multiplexer #(.select(1), .width(16), .disabled("Z"), .enable("false")) multiplexer_1 (
    .in0(\速度初始 ), .in1(16'h1), .out(\速度 ), .sel(comparator_1_lt));
  and and_1 (and_1_out, ~comparator_1_eq, \加速 );  // AND_Gate
  Counter #(.width(16), .max('hffff), .ongoal("wrap"), .trigger("rising"), .behavior("new")) counter_1 (
    .load(comparator_1_lt), .D(16'h1), .Q(\速度初始 ), .clk(or_1_out), .down(and_1_out));  // open: count, carry, clr, preset
  or or_1 (or_1_out, and_1_out, \减速 );

  // Notes on the sheet:
  //   HP
endmodule

module \玩家移动  (
  input  IR1,
  input  IR2,
  input  IR3,
  output RegWrite,
  output MemWrite,
  output [31:0] PC,
  output [31:0] IR,
  output [31:0] RDin,
  output [31:0] MDin,
  output [31:0] LedData
);

  wire ALUeq, ALUge, ALUle, and_1_out, and_2_out, and_3_out, and_5_out, and_6_out, and_7_out, and_8_out, Beq,
       Bne, Btype, CLK, clock_1_out, CLR1, CLR2, CLR3, comparator_1_eq, comparator_2_eq, comparator_3_eq,
       comparator_4_eq, comparator_5_eq, comparator_5_lt, comparator_6_eq, comparator_6_gt, comparator_6_lt,
       d_ff_1_q, d_ff_2_q, d_ff_3_q, d_ff_5_q, ecall, Go, halt, IE, INTR, INTR1, INTR2, INTR3, IR1_t, IR2_t,
       IR3_t, IRA, IRB, IRC, IRHAVE, JAL, JALR, Jtype, MemToReg, nand_1_out, not_1_out, not_2_out, not_3_out,
       or_1_out, or_2_out, or_7_out, or_9_out, or_13_out, or_14_out, or_16_out, or_17_out, RST, Stype, URET,
       W1, W2, W3, \单周期硬布线控制器_1_p13 ;
  wire [1:0] priority_encoder_1_out, priority_encoder_2_out, priority_encoder_3_out, register_2_q;
  wire [3:0] \单周期硬布线控制器_1_p12 ;
  wire [4:0] multiplexer_4_out, multiplexer_5_out;
  wire [12:0] CNT_num;
  wire [15:0] \总周期数 ;
  wire [31:0] ALUres, bit_extender_1_out, bit_extender_2_out, bit_extender_3_out, bit_extender_4_out, Dout,
       IR_PC, MEPC, multiplexer_1_out, multiplexer_3_out, multiplexer_6_out, multiplexer_7_out, PC_4, PC_B,
       PC_J, regifile_1_r1, shifter_1_out, shifter_2_out;

  Button \u_继续运行  (.out(Go));
  Button _1 (.out(IRA));
  Button _2 (.out(IRB));
  Button _3 (.out(IRC));
  LED #(.active("true")) led_1 (.in(W1));
  LED #(.active("true")) led_2 (.in(W2));
  LED #(.active("true")) led_3 (.in(W3));
  Hex_Digit_Display hex_digit_display_1 (.value(LedData[27:24]));  // open: dp
  Hex_Digit_Display hex_digit_display_2 (.value(LedData[31:28]));  // open: dp
  or or_1 (or_1_out, Go, not_1_out);
  not not_1 (not_1_out, halt);
  Hex_Digit_Display hex_digit_display_3 (.value(LedData[23:20]));  // open: dp
  Hex_Digit_Display hex_digit_display_4 (.value(LedData[19:16]));  // open: dp
  Counter #(.width(16), .max('hffff), .ongoal("wrap"), .trigger("rising"), .behavior("new")) counter_1 (
    .count(or_1_out), .Q(\总周期数 ), .clk(CLK));  // open: load, D, carry, clr, preset, down
  Comparator #(.width(16), .mode("twosComplement")) comparator_1 (
    .a(16'h23b), .b(\总周期数 ), .eq(comparator_1_eq));  // open: gt, lt
  Comparator #(.width(16), .mode("twosComplement")) comparator_2 (
    .a(\总周期数 ), .b(16'h1), .eq(comparator_2_eq));  // open: gt, lt
  Comparator #(.width(16), .mode("twosComplement")) comparator_3 (
    .a(\总周期数 ), .b(16'h4), .eq(comparator_3_eq));  // open: gt, lt
  Comparator #(.width(16), .mode("twosComplement")) comparator_4 (
    .a(\总周期数 ), .b(16'h7), .eq(comparator_4_eq));  // open: gt, lt
  Hex_Digit_Display hex_digit_display_5 (.value(LedData[11:8]));  // open: dp
  Hex_Digit_Display hex_digit_display_6 (.value(LedData[15:12]));  // open: dp
  or or_2 (or_2_out, comparator_1_eq, comparator_2_eq);
  assign IRA = or_2_out ? ~CLK : 1'bz;  // Controlled_Inverter controlled_inverter_1
  assign IRB = comparator_3_eq ? ~CLK : 1'bz;  // Controlled_Inverter controlled_inverter_2
  assign IRC = comparator_4_eq ? ~CLK : 1'bz;  // Controlled_Inverter controlled_inverter_3
  Hex_Digit_Display hex_digit_display_7 (.value(LedData[3:0]));  // open: dp
  Hex_Digit_Display hex_digit_display_8 (.value(LedData[7:4]));  // open: dp
  // Probe on \总周期数 
  Pull_Resistor #(.pull(0)) pull_resistor_1 (.node(IRA));
  Pull_Resistor #(.pull(0)) pull_resistor_2 (.node(IRB));
  Pull_Resistor #(.pull(0)) pull_resistor_3 (.node(IRC));
  Priority_Encoder #(.select(2), .disabled("Z")) priority_encoder_1 (
    .in0(INTR1), .in1(INTR2), .in2(INTR3), .out(priority_encoder_1_out));  // open: in3, gs, en_out, en_in
  Priority_Encoder #(.select(2), .disabled("Z")) priority_encoder_2 (
    .in0(1'b1), .in1(JALR), .in2(JAL), .in3(Btype), .out(priority_encoder_2_out));  // open: gs, en_out, en_in
  Multiplexer #(.select(2), .width(32), .disabled("Z"), .enable("false")) multiplexer_1 (
    .in0(PC_4), .in1(ALUres), .in2(PC_J), .in3(PC_B), .out(multiplexer_1_out), .sel(priority_encoder_2_out));
  Multiplexer #(.select(2), .width(32), .disabled("Z"), .enable("false")) multiplexer_2 (
    .in0(32'h30ac), .in1(32'h3150), .in2(32'h31f4), .out(IR_PC), .sel(priority_encoder_1_out));  // open: in3
  or or_3 (IR1_t, IR1, IRA);
  and and_1 (and_1_out, Beq, ALUeq);
  not not_2 (not_2_out, ALUeq);
  and and_2 (and_2_out, not_2_out, Bne);
  Priority_Encoder #(.select(2), .disabled("Z")) priority_encoder_3 (
    .in0(1'b1), .in1(INTR), .in2(URET), .out(priority_encoder_3_out));  // open: in3, gs, en_out, en_in
  or or_4 (W1, INTR1, d_ff_1_q);
  or or_5 (IR2_t, IR2, IRB);
  Register #(.width(32), .trigger("rising"), .Select("low")) register_1 (
    .D(multiplexer_1_out), .en(INTR), .Q(MEPC), .clk(CLK));  // open: clr
  Multiplexer #(.select(2), .width(32), .disabled("Z"), .enable("false")) multiplexer_3 (
    .in0(multiplexer_1_out), .in1(IR_PC), .in2(MEPC), .out(multiplexer_3_out), .sel(priority_encoder_3_out));  // open: in3
  D_Flip_Flop #(.trigger("rising"), .Pre_Clr_Positions("LEGACY"), .NegatePresetClear("false"), .enable("true"), .NewFFLayout("false")) d_ff_1 (
    .clk(IRA), .D(1'b1), .Q(d_ff_1_q), .reset(INTR1));  // open: Qn, preset, en
  Register #(.width(2), .trigger("rising"), .Select("low")) register_2 (
    .D(priority_encoder_1_out), .en(INTR), .Q(register_2_q), .clk(CLK));  // open: clr
  or or_6 (Btype, and_1_out, and_2_out);
  or or_7 (or_7_out, Go, not_3_out);
  not not_3 (not_3_out, halt);
  or or_8 (IRHAVE, INTR1, INTR2, INTR3);
  or or_9 (or_9_out, d_ff_1_q, INTR1);
  Demultiplexer #(.select(2), .width(1), .tristate("false"), .disabled("Z"), .enable("false")) demultiplexer_1 (
    .out0(CLR1), .out1(CLR2), .out2(CLR3), .in(URET), .sel(register_2_q));  // open: out3
  or or_10 (IR3_t, IR3, IRC);
  Register #(.width(32), .trigger("rising"), .Select("low")) u_PC (
    .D(multiplexer_3_out), .en(or_7_out), .Q(PC), .clk(CLK), .clr(RST));
  and and_3 (and_3_out, or_9_out, ~CLR1);  // AND_Gate
  or or_11 (Jtype, JAL, JALR);
  and and_4 (INTR, IE, IRHAVE);
  D_Flip_Flop #(.trigger("rising"), .Pre_Clr_Positions("LEGACY"), .NegatePresetClear("false"), .enable("true"), .NewFFLayout("false")) u_IR1 (
    .clk(CLK), .D(and_3_out), .Q(INTR1));  // open: Qn, preset, en, reset
  // RiscV_Probe riscv_probe_1: pin names not known; wires that end beside it: IR
  Adder #(.width(32)) adder_1 (.a(PC), .b(32'h4), .out(PC_4));  // open: cin, cout
  ROM #(.addrWidth(10), .dataWidth(32), .Select("high")) rom_1 (.addr(PC[11:2]), .data(IR));
  or or_12 (W2, INTR2, d_ff_2_q);
  // 单周期硬布线控制器 单周期硬布线控制器_1: pin names not known; wires that end beside it: JAL, JALR, URET, IR[21], IR[6:2], {IR[30], IR[25], IR[14:12]}, ecall, Beq, Bne, MemToReg, MemWrite, \单周期硬布线控制器_1_p12 , \单周期硬布线控制器_1_p13 , RegWrite, Stype
  Multiplexer #(.select(1), .width(5), .disabled("Z"), .enable("false")) multiplexer_4 (
    .in0(IR[19:15]), .in1(5'b10001), .out(multiplexer_4_out), .sel(ecall));
  Multiplexer #(.select(1), .width(5), .disabled("Z"), .enable("false")) multiplexer_5 (
    .in0(IR[24:20]), .in1(5'b01010), .out(multiplexer_5_out), .sel(ecall));
  assign bit_extender_1_out = {{20{IR[31]}}, IR[31:20]};  // Bit_Extender bit_extender_1
  assign bit_extender_2_out = {{20{IR[31]}}, {IR[31:25], IR[11:7]}};  // Bit_Extender bit_extender_2
  D_Flip_Flop #(.trigger("rising"), .Pre_Clr_Positions("LEGACY"), .NegatePresetClear("false"), .enable("true"), .NewFFLayout("false")) d_ff_2 (
    .clk(IRB), .D(1'b1), .Q(d_ff_2_q), .reset(INTR2));  // open: Qn, preset, en
  Multiplexer #(.select(1), .width(32), .disabled("Z"), .enable("false")) multiplexer_6 (
    .in0(bit_extender_1_out), .in1(bit_extender_2_out), .out(multiplexer_6_out), .sel(Stype));
  assign bit_extender_3_out = {{20{IR[31]}}, {IR[31], IR[7], IR[30:25], IR[11:8]}};  // Bit_Extender bit_extender_3
  assign bit_extender_4_out = {{12{IR[31]}}, {IR[31], IR[19:12], IR[20], IR[30:21]}};  // Bit_Extender bit_extender_4
  or or_13 (or_13_out, d_ff_2_q, INTR2);
  D_Flip_Flop #(.trigger("high"), .Pre_Clr_Positions("LEGACY"), .NegatePresetClear("false"), .enable("true"), .NewFFLayout("false")) d_ff_3 (.Q(d_ff_3_q));  // open: clk, D, Qn, preset, en, reset
  // Probe on 13'hc
  Regifile regifile_1 (
    .Din(RDin), .Clk(CLK), .R1(regifile_1_r1), .R2(MDin), .WE(RegWrite), .W_num(IR[11:7]),
    .R1_num(multiplexer_4_out), .R2_num(multiplexer_5_out));
  Shifter #(.width(32), .shift("ll")) shifter_1 (.in(bit_extender_3_out), .\dist (5'b00001), .out(shifter_1_out));
  Shifter #(.width(32), .shift("ll")) shifter_2 (.in(bit_extender_4_out), .\dist (5'b00001), .out(shifter_2_out));
  and and_5 (and_5_out, or_13_out, ~CLR2);  // AND_Gate
  Comparator #(.width(13), .mode("twosComplement")) comparator_5 (
    .a(CNT_num), .b(13'hc), .eq(comparator_5_eq), .lt(comparator_5_lt));  // open: gt
  Clock #(.highDuration(1), .lowDuration(1)) clock_1 (.out(clock_1_out));
  Multiplexer #(.select(1), .width(32), .disabled("Z"), .enable("false")) multiplexer_7 (
    .in0(MDin), .in1(multiplexer_6_out), .out(multiplexer_7_out), .sel(\单周期硬布线控制器_1_p13 ));
  Adder #(.width(32)) adder_2 (.a(shifter_1_out), .b(PC), .out(PC_B));  // open: cin, cout
  Adder #(.width(32)) adder_3 (.a(shifter_2_out), .b(PC), .out(PC_J));  // open: cin, cout
  D_Flip_Flop #(.trigger("rising"), .Pre_Clr_Positions("LEGACY"), .NegatePresetClear("false"), .enable("true"), .NewFFLayout("false")) u_IR2 (
    .clk(CLK), .D(and_5_out), .Q(INTR2));  // open: Qn, preset, en, reset
  nand nand_1 (nand_1_out, d_ff_3_q, comparator_5_eq);
  Counter #(.width(13), .max('h1fff), .ongoal("stay"), .trigger("rising"), .behavior("old")) counter_2 (
    .count(comparator_5_lt), .Q(CNT_num), .clk(clock_1_out));  // open: load, D, carry, clr, preset
  ALU alu_1 (
    .X(regifile_1_r1), .Y(multiplexer_7_out), .AluOP(\单周期硬布线控制器_1_p12 ), .Equal(ALUeq), .Result(ALUres),
    .out_4(ALUge), .out_6(ALUle));  // open: Result_2
  assign CLK = nand_1_out ? clock_1_out : 1'bz;  // Controlled_Buffer controlled_buffer_1
  Comparator #(.width(32), .mode("twosComplement")) comparator_6 (
    .a(32'h22), .b(regifile_1_r1), .gt(comparator_6_gt), .eq(comparator_6_eq), .lt(comparator_6_lt));
  or or_14 (or_14_out, ~IRHAVE, URET);  // OR_Gate
  Pull_Resistor #(.pull(1)) pull_resistor_4 (.node(CLK));
  Register #(.width(32), .trigger("rising"), .Select("low")) register_3 (
    .D(MDin), .en(and_6_out), .Q(LedData), .clk(CLK));  // open: clr
  and and_6 (and_6_out, ecall, comparator_6_eq);
  or or_15 (W3, INTR3, d_ff_5_q);
  and and_7 (and_7_out, or_16_out, ecall);
  or or_16 (or_16_out, comparator_6_gt, comparator_6_lt);
  D_Flip_Flop #(.trigger("rising"), .Pre_Clr_Positions("LEGACY"), .NegatePresetClear("false"), .enable("true"), .NewFFLayout("true")) d_ff_4 (
    .clk(CLK), .D(or_14_out), .Q(IE));  // open: Qn, preset, en, reset
  D_Flip_Flop #(.trigger("rising"), .Pre_Clr_Positions("LEGACY"), .NegatePresetClear("false"), .enable("true"), .NewFFLayout("false")) d_ff_5 (
    .clk(IRC), .D(1'b1), .Q(d_ff_5_q), .reset(INTR3));  // open: Qn, preset, en
  RAM #(.addrWidth(10), .dataWidth(32), .bus("separate"), .Select("high")) ram_1 (
    .addr(ALUres[11:2]), .din(MDin), .data(Dout), .str(MemWrite), .sel(1'b1), .clk(CLK), .ld(1'b1));  // open: clr
  Multiplexer #(.select(2), .width(32), .disabled("Z"), .enable("false")) multiplexer_8 (
    .in0(ALUres), .in1(Dout), .in2(PC_4), .in3(PC_4), .out(RDin), .sel({Jtype, MemToReg}));
  or or_17 (or_17_out, d_ff_5_q, INTR3);
  D_Flip_Flop #(.trigger("falling"), .Pre_Clr_Positions("ABOVE_BELOW"), .NegatePresetClear("false"), .enable("true"), .NewFFLayout("true")) d_ff_6 (
    .clk(CLK), .D(1'b1), .Q(halt), .en(and_7_out), .reset(Go));  // open: Qn, preset
  and and_8 (and_8_out, or_17_out, ~CLR3);  // AND_Gate
  D_Flip_Flop #(.trigger("rising"), .Pre_Clr_Positions("LEGACY"), .NegatePresetClear("false"), .enable("true"), .NewFFLayout("false")) u_IR3 (
    .clk(CLK), .D(and_8_out), .Q(INTR3));  // open: Qn, preset, en, reset

  // Notes on the sheet:
  //   中断源
  //   中断等待指示
  //   总复位信号应将除ROM以外所有存储组件全部清零
  //   单级中断测试信号模拟器
  //   数码管输出
  //   数码管输出应该用寄存器锁存，否则显示数据只能一闪而过
  //   中断响应阶段
  //   指令探针
  //   指令存储器
  //   中断响应
  //   为方便自动评测，需要输出PC，IR，寄存器堆写如数据RDin
  //   RAM写使能MemWrite、RAM写入数据MDin等信号
  //   指令字
  //   contents of rom_1 (hex, n*v repeats v):
  //   7d000113 100413 1f41993 41f9d993 433 c00913 800b13 140413 f47413 800293 100313 499993 89e9b3 1300533
  //   2200893 73 406282b3 fe0294e3 140413 f00f93 1f47433 1c41413 800293 100313 49d993 89e9b3 1300533
  //   2200893 73 406282b3 fe0294e3 1c45413 406b0b33 b0463 f95ff06f 2b3 fff2c293 1029293 fff2e293 500533
  //   2200893 73 f5dff06f 1112023 410113 a12023 410113 812023 410113 1312023 410113 1412023 410113 1512023
  //   410113 1612023 410113 100b13 300a13 100a93 1600433 441413 14469b3 1300533 2200893 73 fe0416e3
  //   415a0a33 fe0a10e3 ffc10113 12b03 ffc10113 12a83 ffc10113 12a03 ffc10113 12983 ffc10113 12403
  //   ffc10113 12503 ffc10113 12883 200073 1112023 410113 a12023 410113 812023 410113 1312023 410113
  //   1412023 410113 1512023 410113 1612023 410113 200b13 300a13 100a93 1600433 441413 14469b3 1300533
  //   2200893 73 fe0416e3 415a0a33 fe0a10e3 ffc10113 12b03 ffc10113 12a83 ffc10113 12a03 ffc10113 12983
  //   ffc10113 12403 ffc10113 12503 ffc10113 12883 200073 1112023 410113 a12023 410113 812023 410113
  //   1312023 410113 1412023 410113 1512023 410113 1612023 410113 300b13 300a13 100a93 1600433 441413
  //   14469b3 1300533 2200893 73 fe0416e3 415a0a33 fe0a10e3 ffc10113 12b03 ffc10113 12a83 ffc10113 12a03
  //   ffc10113 12983 ffc10113 12403 ffc10113 12503 ffc10113 12883 200073
  //   URET
  //   Beq
  //   Bne
  //   MemToReg
  //   MemWrite
  //   AluOP
  //   AluSrcB
  //   RegWrite
  //   控制位
  //   暂停节拍，不能为0
  //   戳工具置1进入计数暂停模式，ctrl+k时钟自动运行到对应节拍暂停
  //   ctrl+k关闭时钟连续运行，将控制位置零，进入单步调试模式调试
  //   中断使能位(用于开关中断)
  //   可计数暂停的时钟源
  //   数据存储器
  //   判断中断使能
endmodule

module \障碍下落  (
  input  RST,
  input  [15:0] \下落速度 ,
  input  CLK
);

  wire CLK_t;

  \频率控制电路  \u_频率控制电路_1  (.\延缓倍数 (\下落速度 ), .\现CLK (CLK_t), .\原CLK (CLK), .RST(RST));
endmodule

// 单周期硬布线控制器
module \单周期硬布线控制器  (
  input  [5:0] OP,
  input  [5:0] Funct,
  input  in_3,
  output [3:0] ALU_OP,
  output MemToReg,
  output MemWrite,
  output ALU_SRC,
  output RegWrite,
  output SysCALL,
  output SignedExt,
  output RegDst,
  output Beq,
  output Bne,
  output JR,
  output JMP,
  output JAL,
  output BLTZ,
  output LH,
  output LUI,
  output SRLV,
  output SET_IE,
  output Clear_IR
);

  \运算控制器自动生成  \u_运算控制器自动生成_1  (
    .OP0(OP[0]), .OP1(OP[1]), .OP2(OP[2]), .OP3(OP[3]), .OP4(OP[4]), .OP5(OP[5]), .F0(Funct[0]),
    .F1(Funct[1]), .F2(Funct[2]), .F3(Funct[3]), .F4(Funct[4]), .F5(Funct[5]), .S0(ALU_OP[0]),
    .S1(ALU_OP[1]), .S2(ALU_OP[2]), .S3(ALU_OP[3]));
  \控制信号自动生成  \u_控制信号自动生成_1  (
    .OP0(OP[0]), .MemToReg(MemToReg), .OP1(OP[1]), .OP2(OP[2]), .MemWrite(MemWrite), .OP3(OP[3]),
    .OP4(OP[4]), .OP5(OP[5]), .F0(Funct[0]), .F1(Funct[1]), .ALU_SRC(ALU_SRC), .F2(Funct[2]), .F3(Funct[3]),
    .F4(Funct[4]), .F5(Funct[5]), .RegWrite(RegWrite), .SysCALL(SysCALL), .SignedExt(SignedExt),
    .RegDst(RegDst), .BEQ(Beq), .BNE(Bne), .JR(JR), .JUMP(JMP), .JAL(JAL));
  \新增控制信号自动生成  \u_新增控制信号自动生成_1  (
    .OP0(OP[0]), .OP1(OP[1]), .OP2(OP[2]), .OP3(OP[3]), .OP4(OP[4]), .OP5(OP[5]), .F0(Funct[0]),
    .F1(Funct[1]), .F2(Funct[2]), .F3(Funct[3]), .F4(Funct[4]), .F5(Funct[5]), .BLTZ(BLTZ), .LH(LH),
    .LUI(LUI), .SRLV(SRLV), .SET_IE(SET_IE), .Clear_IR(Clear_IR));

  // Other names for the same wires on the sheet: IR21 = in_3; OP_CODE[5:0] = OP

  // Notes on the sheet:
  //   运算器控制器，根据指令生成运算器功能选择信号
  //   控制信号生成，产生数据通路需要的其他控制信号
endmodule

// 运算器控制器
module \运算控制器自动生成  (
  input  OP0,
  input  OP1,
  input  OP2,
  input  OP3,
  input  OP4,
  input  OP5,
  input  F0,
  input  F1,
  input  F2,
  input  F3,
  input  F4,
  input  F5,
  output S0,
  output S1,
  output S2,
  output S3
);

  wire and_1_out, and_2_out, and_3_out, and_4_out, and_5_out, and_6_out, and_7_out, and_8_out, and_9_out,
       and_10_out, and_11_out, and_12_out, and_13_out, and_14_out, and_15_out, and_16_out, and_17_out,
       and_18_out, and_19_out, and_20_out, and_21_out, and_22_out, and_23_out, and_24_out, and_25_out,
       and_26_out, and_27_out, and_28_out, not_1_out, not_2_out, not_3_out, not_4_out, not_5_out, not_6_out,
       not_7_out, not_8_out, not_9_out, not_10_out, not_11_out, not_12_out, not_13_out, not_14_out,
       not_15_out, not_16_out, not_17_out, not_18_out, not_19_out, not_20_out, not_21_out, not_22_out,
       not_23_out, not_24_out, not_25_out, not_26_out, not_27_out, not_28_out, not_29_out, not_30_out,
       not_31_out, not_32_out, not_33_out, not_34_out, not_35_out, not_36_out, not_37_out, not_38_out,
       not_39_out, not_40_out, not_41_out, not_42_out, not_43_out, not_44_out, not_45_out, not_46_out,
       not_47_out, not_48_out, not_49_out, not_50_out, not_51_out, not_52_out, not_53_out, not_54_out,
       not_55_out, not_56_out, not_57_out, not_58_out, not_59_out, not_60_out, not_61_out, not_62_out,
       not_63_out, not_64_out, not_65_out, not_66_out, not_67_out, not_68_out, not_69_out, not_70_out,
       not_71_out, not_72_out, not_73_out, not_74_out, not_75_out, not_76_out, not_77_out, not_78_out,
       not_79_out, not_80_out, not_81_out, not_82_out, not_83_out, not_84_out, not_85_out, not_86_out,
       not_87_out, not_88_out, not_89_out, not_90_out, not_91_out, not_92_out, not_93_out, not_94_out,
       not_95_out, not_96_out, not_97_out, not_98_out, not_99_out, not_100_out, not_101_out, not_102_out,
       not_103_out, not_104_out, not_105_out, not_106_out, not_107_out, not_108_out, not_109_out,
       not_110_out, not_111_out, not_112_out, not_113_out, not_114_out, not_115_out, not_116_out,
       not_117_out, not_118_out, not_119_out, not_120_out, not_121_out, not_122_out, not_123_out,
       not_124_out, not_125_out, not_126_out, not_127_out, not_128_out, not_129_out, not_130_out,
       not_131_out, not_132_out, not_133_out, not_134_out, not_135_out, not_136_out, not_137_out,
       not_138_out, not_139_out, not_140_out, not_141_out, not_142_out, not_143_out, not_144_out,
       not_145_out, not_146_out, not_147_out, not_148_out, not_149_out, not_150_out, not_151_out,
       not_152_out, not_153_out, not_154_out, not_155_out, not_156_out, not_157_out, not_158_out,
       not_159_out, not_160_out, not_161_out, not_162_out, not_163_out, not_164_out, not_165_out,
       not_166_out, not_167_out, not_168_out, not_169_out, not_170_out, not_171_out, not_172_out;

  not not_1 (not_1_out, OP0);
  not not_2 (not_2_out, OP1);
  not not_3 (not_3_out, OP2);
  not not_4 (not_4_out, OP4);
  not not_5 (not_5_out, OP5);
  not not_6 (not_6_out, F1);
  not not_7 (not_7_out, F2);
  not not_8 (not_8_out, F3);
  not not_9 (not_9_out, F4);
  not not_10 (not_10_out, OP0);
  not not_11 (not_11_out, OP1);
  not not_12 (not_12_out, OP2);
  not not_13 (not_13_out, OP4);
  not not_14 (not_14_out, OP5);
  not not_15 (not_15_out, F0);
  not not_16 (not_16_out, F3);
  not not_17 (not_17_out, F4);
  not not_18 (not_18_out, OP0);
  not not_19 (not_19_out, OP1);
  not not_20 (not_20_out, OP2);
  not not_21 (not_21_out, OP4);
  not not_22 (not_22_out, OP5);
  not not_23 (not_23_out, F0);
  not not_24 (not_24_out, F2);
  not not_25 (not_25_out, F4);
  not not_26 (not_26_out, OP0);
  not not_27 (not_27_out, OP1);
  not not_28 (not_28_out, OP2);
  not not_29 (not_29_out, OP4);
  not not_30 (not_30_out, OP5);
  not not_31 (not_31_out, F2);
  not not_32 (not_32_out, F3);
  not not_33 (not_33_out, F4);
  not not_34 (not_34_out, F5);
  not not_35 (not_35_out, OP0);
  not not_36 (not_36_out, OP1);
  not not_37 (not_37_out, OP4);
  not not_38 (not_38_out, OP5);
  not not_39 (not_39_out, OP0);
  not not_40 (not_40_out, OP2);
  not not_41 (not_41_out, OP4);
  not not_42 (not_42_out, OP5);
  not not_43 (not_43_out, OP1);
  not not_44 (not_44_out, OP2);
  not not_45 (not_45_out, OP4);
  not not_46 (not_46_out, OP5);
  not not_47 (not_47_out, OP2);
  not not_48 (not_48_out, OP3);
  not not_49 (not_49_out, OP4);
  not not_50 (not_50_out, OP2);
  not not_51 (not_51_out, OP4);
  not not_52 (not_52_out, OP0);
  not not_53 (not_53_out, OP1);
  not not_54 (not_54_out, OP2);
  not not_55 (not_55_out, OP3);
  not not_56 (not_56_out, OP4);
  not not_57 (not_57_out, OP5);
  not not_58 (not_58_out, F0);
  not not_59 (not_59_out, F1);
  not not_60 (not_60_out, F3);
  not not_61 (not_61_out, F4);
  not not_62 (not_62_out, OP0);
  not not_63 (not_63_out, OP1);
  not not_64 (not_64_out, OP2);
  not not_65 (not_65_out, OP3);
  not not_66 (not_66_out, OP4);
  not not_67 (not_67_out, OP5);
  not not_68 (not_68_out, F0);
  not not_69 (not_69_out, F3);
  not not_70 (not_70_out, F4);
  not not_71 (not_71_out, F5);
  not not_72 (not_72_out, OP0);
  not not_73 (not_73_out, OP1);
  not not_74 (not_74_out, OP2);
  not not_75 (not_75_out, OP3);
  not not_76 (not_76_out, OP4);
  not not_77 (not_77_out, OP5);
  not not_78 (not_78_out, F0);
  not not_79 (not_79_out, F2);
  not not_80 (not_80_out, F4);
  not not_81 (not_81_out, OP0);
  not not_82 (not_82_out, OP1);
  not not_83 (not_83_out, OP2);
  not not_84 (not_84_out, OP3);
  not not_85 (not_85_out, OP4);
  not not_86 (not_86_out, OP5);
  not not_87 (not_87_out, F3);
  not not_88 (not_88_out, F4);
  not not_89 (not_89_out, OP0);
  not not_90 (not_90_out, OP1);
  not not_91 (not_91_out, OP4);
  not not_92 (not_92_out, OP5);
  not not_93 (not_93_out, OP0);
  not not_94 (not_94_out, OP2);
  not not_95 (not_95_out, OP4);
  not not_96 (not_96_out, OP5);
  not not_97 (not_97_out, OP0);
  not not_98 (not_98_out, OP1);
  not not_99 (not_99_out, OP2);
  not not_100 (not_100_out, OP4);
  not not_101 (not_101_out, OP5);
  not not_102 (not_102_out, F0);
  not not_103 (not_103_out, F1);
  not not_104 (not_104_out, F3);
  not not_105 (not_105_out, F4);
  not not_106 (not_106_out, OP0);
  not not_107 (not_107_out, OP1);
  not not_108 (not_108_out, OP2);
  not not_109 (not_109_out, OP4);
  not not_110 (not_110_out, OP5);
  not not_111 (not_111_out, F0);
  not not_112 (not_112_out, F2);
  not not_113 (not_113_out, F3);
  not not_114 (not_114_out, F4);
  not not_115 (not_115_out, OP0);
  not not_116 (not_116_out, OP1);
  not not_117 (not_117_out, OP2);
  not not_118 (not_118_out, OP4);
  not not_119 (not_119_out, OP5);
  not not_120 (not_120_out, F1);
  not not_121 (not_121_out, F2);
  not not_122 (not_122_out, F3);
  not not_123 (not_123_out, F4);
  not not_124 (not_124_out, OP0);
  not not_125 (not_125_out, OP1);
  not not_126 (not_126_out, OP2);
  not not_127 (not_127_out, OP4);
  not not_128 (not_128_out, OP5);
  not not_129 (not_129_out, F2);
  not not_130 (not_130_out, F4);
  not not_131 (not_131_out, OP0);
  not not_132 (not_132_out, OP1);
  not not_133 (not_133_out, OP4);
  not not_134 (not_134_out, OP5);
  not not_135 (not_135_out, OP2);
  not not_136 (not_136_out, OP3);
  not not_137 (not_137_out, OP4);
  not not_138 (not_138_out, OP2);
  not not_139 (not_139_out, OP4);
  not not_140 (not_140_out, OP5);
  not not_141 (not_141_out, OP2);
  not not_142 (not_142_out, OP4);
  not not_143 (not_143_out, OP0);
  not not_144 (not_144_out, OP1);
  not not_145 (not_145_out, OP2);
  not not_146 (not_146_out, OP3);
  not not_147 (not_147_out, OP4);
  not not_148 (not_148_out, OP5);
  not not_149 (not_149_out, F2);
  not not_150 (not_150_out, F4);
  not not_151 (not_151_out, OP0);
  not not_152 (not_152_out, OP1);
  not not_153 (not_153_out, OP2);
  not not_154 (not_154_out, OP3);
  not not_155 (not_155_out, OP4);
  not not_156 (not_156_out, OP5);
  not not_157 (not_157_out, F3);
  not not_158 (not_158_out, F4);
  not not_159 (not_159_out, OP0);
  not not_160 (not_160_out, OP1);
  not not_161 (not_161_out, OP2);
  not not_162 (not_162_out, OP3);
  not not_163 (not_163_out, OP4);
  not not_164 (not_164_out, OP5);
  not not_165 (not_165_out, F3);
  not not_166 (not_166_out, F4);
  not not_167 (not_167_out, OP2);
  not not_168 (not_168_out, OP4);
  not not_169 (not_169_out, OP5);
  not not_170 (not_170_out, OP1);
  not not_171 (not_171_out, OP4);
  not not_172 (not_172_out, OP5);
  and and_1 (and_1_out, not_1_out, not_2_out, not_3_out, not_4_out, not_5_out, not_6_out, not_7_out, not_8_out, not_9_out, F5);
  and and_2 (and_2_out, not_10_out, not_11_out, not_12_out, not_13_out, not_14_out, not_15_out, F2, not_16_out, not_17_out, F5);
  and and_3 (and_3_out, not_18_out, not_19_out, not_20_out, not_21_out, not_22_out, not_23_out, F1, not_24_out, F3, not_25_out, F5);
  and and_4 (and_4_out, not_26_out, not_27_out, not_28_out, not_29_out, not_30_out, F0, F1, not_31_out, not_32_out, not_33_out, not_34_out);
  and and_5 (and_5_out, not_35_out, not_36_out, OP3, not_37_out, not_38_out);
  and and_6 (and_6_out, not_39_out, not_40_out, OP3, not_41_out, not_42_out);
  and and_7 (and_7_out, not_43_out, not_44_out, OP3, not_45_out, not_46_out);
  and and_8 (and_8_out, OP0, not_47_out, not_48_out, not_49_out, OP5);
  and and_9 (and_9_out, OP0, OP1, not_50_out, not_51_out, OP5);
  and and_10 (and_10_out, not_52_out, not_53_out, not_54_out, not_55_out, not_56_out, not_57_out, not_58_out, not_59_out, F2, not_60_out, not_61_out, F5);
  and and_11 (and_11_out, not_62_out, not_63_out, not_64_out, not_65_out, not_66_out, not_67_out, not_68_out, F1, not_69_out, not_70_out, not_71_out);
  and and_12 (and_12_out, not_72_out, not_73_out, not_74_out, not_75_out, not_76_out, not_77_out, not_78_out, F1, not_79_out, not_80_out, F5);
  and and_13 (and_13_out, not_81_out, not_82_out, not_83_out, not_84_out, not_85_out, not_86_out, F0, F1, F2, not_87_out, not_88_out, F5);
  and and_14 (and_14_out, not_89_out, not_90_out, OP2, OP3, not_91_out, not_92_out);
  and and_15 (and_15_out, not_93_out, OP1, not_94_out, OP3, not_95_out, not_96_out);
  and and_16 (and_16_out, not_97_out, not_98_out, not_99_out, not_100_out, not_101_out, not_102_out, not_103_out, not_104_out, not_105_out, F5);
  and and_17 (and_17_out, not_106_out, not_107_out, not_108_out, not_109_out, not_110_out, not_111_out, not_112_out, not_113_out, not_114_out, F5);
  and and_18 (and_18_out, not_115_out, not_116_out, not_117_out, not_118_out, not_119_out, not_120_out, not_121_out, not_122_out, not_123_out, F5);
  and and_19 (and_19_out, not_124_out, not_125_out, not_126_out, not_127_out, not_128_out, F0, F1, not_129_out, F3, not_130_out, F5);
  and and_20 (and_20_out, not_131_out, not_132_out, OP3, not_133_out, not_134_out);
  and and_21 (and_21_out, OP0, not_135_out, not_136_out, not_137_out, OP5);
  and and_22 (and_22_out, OP0, not_138_out, OP3, not_139_out, not_140_out);
  and and_23 (and_23_out, OP0, OP1, not_141_out, not_142_out, OP5);
  and and_24 (and_24_out, not_143_out, not_144_out, not_145_out, not_146_out, not_147_out, not_148_out, F1, not_149_out, F3, not_150_out, F5);
  and and_25 (and_25_out, not_151_out, not_152_out, not_153_out, not_154_out, not_155_out, not_156_out, F1, F2, not_157_out, not_158_out, F5);
  and and_26 (and_26_out, not_159_out, not_160_out, not_161_out, not_162_out, not_163_out, not_164_out, F0, F2, not_165_out, not_166_out, F5);
  and and_27 (and_27_out, OP1, not_167_out, OP3, not_168_out, not_169_out);
  and and_28 (and_28_out, OP0, not_170_out, OP2, OP3, not_171_out, not_172_out);
  or or_1 (S0, and_1_out, and_2_out, and_3_out, and_4_out, and_5_out, and_6_out, and_7_out, and_8_out, and_9_out);
  or or_2 (S1, and_10_out, and_11_out, and_12_out, and_13_out, and_14_out, and_15_out);
  or or_3 (S2, and_16_out, and_17_out, and_18_out, and_19_out, and_20_out, and_21_out, and_22_out, and_23_out);
  or or_4 (S3, and_24_out, and_25_out, and_26_out, and_27_out, and_28_out);
endmodule

// 控制信号生成
module \控制信号自动生成  (
  input  OP0,
  input  OP1,
  input  OP2,
  input  OP3,
  input  OP4,
  input  OP5,
  input  F0,
  input  F1,
  input  F2,
  input  F3,
  input  F4,
  input  F5,
  output MemToReg,
  output MemWrite,
  output ALU_SRC,
  output RegWrite,
  output SysCALL,
  output SignedExt,
  output RegDst,
  output BEQ,
  output BNE,
  output JR,
  output JUMP,
  output JAL
);

  wire and_3_out, and_4_out, and_5_out, and_6_out, and_7_out, and_8_out, and_9_out, and_10_out, and_11_out,
       and_12_out, and_13_out, and_14_out, and_15_out, and_16_out, and_18_out, and_19_out, and_20_out,
       and_21_out, and_22_out, and_23_out, and_24_out, and_25_out, not_1_out, not_2_out, not_3_out,
       not_4_out, not_5_out, not_6_out, not_7_out, not_8_out, not_9_out, not_10_out, not_11_out, not_12_out,
       not_13_out, not_14_out, not_15_out, not_16_out, not_17_out, not_18_out, not_19_out, not_20_out,
       not_21_out, not_22_out, not_23_out, not_24_out, not_25_out, not_26_out, not_27_out, not_28_out,
       not_29_out, not_30_out, not_31_out, not_32_out, not_33_out, not_34_out, not_35_out, not_36_out,
       not_37_out, not_38_out, not_39_out, not_40_out, not_41_out, not_42_out, not_43_out, not_44_out,
       not_45_out, not_46_out, not_47_out, not_48_out, not_49_out, not_50_out, not_51_out, not_52_out,
       not_53_out, not_54_out, not_55_out, not_56_out, not_57_out, not_58_out, not_59_out, not_60_out,
       not_61_out, not_62_out, not_63_out, not_64_out, not_65_out, not_66_out, not_67_out, not_68_out,
       not_69_out, not_70_out, not_71_out, not_72_out, not_73_out, not_74_out, not_75_out, not_76_out,
       not_77_out, not_78_out, not_79_out, not_80_out, not_81_out, not_82_out, not_83_out, not_84_out,
       not_85_out, not_86_out, not_87_out, not_88_out, not_89_out, not_90_out, not_91_out, not_92_out,
       not_93_out, not_94_out, not_95_out, not_96_out, not_97_out, not_98_out, not_99_out, not_100_out,
       not_101_out, not_102_out, not_103_out, not_104_out, not_105_out, not_106_out, not_107_out,
       not_108_out, not_109_out, not_110_out, not_111_out, not_112_out, not_113_out, not_114_out,
       not_115_out, not_116_out, not_117_out, not_118_out, not_119_out, not_120_out, not_121_out,
       not_122_out, not_123_out, not_124_out, not_125_out, not_126_out, not_127_out, not_128_out,
       not_129_out, not_130_out, not_131_out, not_132_out, not_133_out, not_134_out, not_135_out,
       not_136_out, not_137_out, not_138_out, not_139_out, not_140_out, not_141_out, not_142_out,
       not_143_out, not_144_out, not_145_out, not_146_out, not_147_out, not_148_out, not_149_out,
       not_150_out, not_151_out, not_152_out, not_153_out, not_154_out, not_155_out, not_156_out,
       not_157_out, not_158_out, not_159_out, not_160_out;

  not not_1 (not_1_out, OP2);
  not not_2 (not_2_out, OP3);
  not not_3 (not_3_out, OP4);
  not not_4 (not_4_out, OP2);
  not not_5 (not_5_out, OP4);
  not not_6 (not_6_out, OP1);
  not not_7 (not_7_out, OP4);
  not not_8 (not_8_out, OP5);
  not not_9 (not_9_out, OP2);
  not not_10 (not_10_out, OP4);
  not not_11 (not_11_out, OP5);
  not not_12 (not_12_out, OP2);
  not not_13 (not_13_out, OP3);
  not not_14 (not_14_out, OP4);
  not not_15 (not_15_out, OP2);
  not not_16 (not_16_out, OP4);
  not not_17 (not_17_out, OP0);
  not not_18 (not_18_out, OP1);
  not not_19 (not_19_out, OP2);
  not not_20 (not_20_out, OP4);
  not not_21 (not_21_out, OP5);
  not not_22 (not_22_out, F0);
  not not_23 (not_23_out, F3);
  not not_24 (not_24_out, F4);
  not not_25 (not_25_out, OP0);
  not not_26 (not_26_out, OP1);
  not not_27 (not_27_out, OP2);
  not not_28 (not_28_out, OP4);
  not not_29 (not_29_out, OP5);
  not not_30 (not_30_out, F1);
  not not_31 (not_31_out, F3);
  not not_32 (not_32_out, F4);
  not not_33 (not_33_out, OP0);
  not not_34 (not_34_out, OP1);
  not not_35 (not_35_out, OP2);
  not not_36 (not_36_out, OP4);
  not not_37 (not_37_out, OP5);
  not not_38 (not_38_out, F3);
  not not_39 (not_39_out, F4);
  not not_40 (not_40_out, OP0);
  not not_41 (not_41_out, OP1);
  not not_42 (not_42_out, OP2);
  not not_43 (not_43_out, OP4);
  not not_44 (not_44_out, OP5);
  not not_45 (not_45_out, F2);
  not not_46 (not_46_out, F3);
  not not_47 (not_47_out, F4);
  not not_48 (not_48_out, F5);
  not not_49 (not_49_out, OP0);
  not not_50 (not_50_out, OP1);
  not not_51 (not_51_out, OP2);
  not not_52 (not_52_out, OP4);
  not not_53 (not_53_out, OP5);
  not not_54 (not_54_out, F2);
  not not_55 (not_55_out, F4);
  not not_56 (not_56_out, OP1);
  not not_57 (not_57_out, OP4);
  not not_58 (not_58_out, OP5);
  not not_59 (not_59_out, OP2);
  not not_60 (not_60_out, OP4);
  not not_61 (not_61_out, OP5);
  not not_62 (not_62_out, OP2);
  not not_63 (not_63_out, OP3);
  not not_64 (not_64_out, OP4);
  not not_65 (not_65_out, OP4);
  not not_66 (not_66_out, OP5);
  not not_67 (not_67_out, OP2);
  not not_68 (not_68_out, OP3);
  not not_69 (not_69_out, OP4);
  not not_70 (not_70_out, OP0);
  not not_71 (not_71_out, OP1);
  not not_72 (not_72_out, OP2);
  not not_73 (not_73_out, OP3);
  not not_74 (not_74_out, OP4);
  not not_75 (not_75_out, OP5);
  not not_76 (not_76_out, F0);
  not not_77 (not_77_out, F1);
  not not_78 (not_78_out, F4);
  not not_79 (not_79_out, F5);
  not not_80 (not_80_out, OP2);
  not not_81 (not_81_out, OP4);
  not not_82 (not_82_out, OP5);
  not not_83 (not_83_out, OP2);
  not not_84 (not_84_out, OP3);
  not not_85 (not_85_out, OP4);
  not not_86 (not_86_out, OP2);
  not not_87 (not_87_out, OP4);
  not not_88 (not_88_out, OP0);
  not not_89 (not_89_out, OP1);
  not not_90 (not_90_out, OP2);
  not not_91 (not_91_out, OP3);
  not not_92 (not_92_out, OP4);
  not not_93 (not_93_out, OP5);
  not not_94 (not_94_out, F0);
  not not_95 (not_95_out, F3);
  not not_96 (not_96_out, F4);
  not not_97 (not_97_out, OP0);
  not not_98 (not_98_out, OP1);
  not not_99 (not_99_out, OP2);
  not not_100 (not_100_out, OP3);
  not not_101 (not_101_out, OP4);
  not not_102 (not_102_out, OP5);
  not not_103 (not_103_out, F1);
  not not_104 (not_104_out, F3);
  not not_105 (not_105_out, F4);
  not not_106 (not_106_out, OP0);
  not not_107 (not_107_out, OP1);
  not not_108 (not_108_out, OP2);
  not not_109 (not_109_out, OP3);
  not not_110 (not_110_out, OP4);
  not not_111 (not_111_out, OP5);
  not not_112 (not_112_out, F3);
  not not_113 (not_113_out, F4);
  not not_114 (not_114_out, OP0);
  not not_115 (not_115_out, OP1);
  not not_116 (not_116_out, OP2);
  not not_117 (not_117_out, OP3);
  not not_118 (not_118_out, OP4);
  not not_119 (not_119_out, OP5);
  not not_120 (not_120_out, F2);
  not not_121 (not_121_out, F3);
  not not_122 (not_122_out, F4);
  not not_123 (not_123_out, F5);
  not not_124 (not_124_out, OP0);
  not not_125 (not_125_out, OP1);
  not not_126 (not_126_out, OP2);
  not not_127 (not_127_out, OP3);
  not not_128 (not_128_out, OP4);
  not not_129 (not_129_out, OP5);
  not not_130 (not_130_out, F2);
  not not_131 (not_131_out, F4);
  not not_132 (not_132_out, OP0);
  not not_133 (not_133_out, OP1);
  not not_134 (not_134_out, OP3);
  not not_135 (not_135_out, OP4);
  not not_136 (not_136_out, OP5);
  not not_137 (not_137_out, OP1);
  not not_138 (not_138_out, OP3);
  not not_139 (not_139_out, OP4);
  not not_140 (not_140_out, OP5);
  not not_141 (not_141_out, OP0);
  not not_142 (not_142_out, OP1);
  not not_143 (not_143_out, OP2);
  not not_144 (not_144_out, OP3);
  not not_145 (not_145_out, OP4);
  not not_146 (not_146_out, OP5);
  not not_147 (not_147_out, F0);
  not not_148 (not_148_out, F1);
  not not_149 (not_149_out, F2);
  not not_150 (not_150_out, F4);
  not not_151 (not_151_out, F5);
  not not_152 (not_152_out, OP0);
  not not_153 (not_153_out, OP2);
  not not_154 (not_154_out, OP3);
  not not_155 (not_155_out, OP4);
  not not_156 (not_156_out, OP5);
  not not_157 (not_157_out, OP2);
  not not_158 (not_158_out, OP3);
  not not_159 (not_159_out, OP4);
  not not_160 (not_160_out, OP5);
  and and_1 (MemToReg, OP0, OP1, not_1_out, not_2_out, not_3_out, OP5);
  and and_2 (MemWrite, OP0, OP1, not_4_out, OP3, not_5_out, OP5);
  and and_3 (and_3_out, not_6_out, OP3, not_7_out, not_8_out);
  and and_4 (and_4_out, not_9_out, OP3, not_10_out, not_11_out);
  and and_5 (and_5_out, OP0, not_12_out, not_13_out, not_14_out, OP5);
  and and_6 (and_6_out, OP0, OP1, not_15_out, OP3, not_16_out);
  and and_7 (and_7_out, not_17_out, not_18_out, not_19_out, not_20_out, not_21_out, not_22_out, not_23_out, not_24_out);
  and and_8 (and_8_out, not_25_out, not_26_out, not_27_out, not_28_out, not_29_out, not_30_out, not_31_out, not_32_out, F5);
  and and_9 (and_9_out, not_33_out, not_34_out, not_35_out, not_36_out, not_37_out, F2, not_38_out, not_39_out, F5);
  and and_10 (and_10_out, not_40_out, not_41_out, not_42_out, not_43_out, not_44_out, F1, not_45_out, not_46_out, not_47_out, not_48_out);
  and and_11 (and_11_out, not_49_out, not_50_out, not_51_out, not_52_out, not_53_out, F1, not_54_out, F3, not_55_out, F5);
  and and_12 (and_12_out, not_56_out, OP3, not_57_out, not_58_out);
  and and_13 (and_13_out, not_59_out, OP3, not_60_out, not_61_out);
  and and_14 (and_14_out, OP0, not_62_out, not_63_out, not_64_out, OP5);
  and and_15 (and_15_out, OP0, OP3, not_65_out, not_66_out);
  and and_16 (and_16_out, OP0, OP1, not_67_out, not_68_out, not_69_out);
  and and_17 (SysCALL, not_70_out, not_71_out, not_72_out, not_73_out, not_74_out, not_75_out, not_76_out, not_77_out, F2, F3, not_78_out, not_79_out);
  and and_18 (and_18_out, not_80_out, OP3, not_81_out, not_82_out);
  or or_1 (SignedExt, and_18_out, and_19_out, and_20_out);
  and and_19 (and_19_out, OP0, not_83_out, not_84_out, not_85_out, OP5);
  and and_20 (and_20_out, OP0, OP1, not_86_out, not_87_out, OP5);
  and and_21 (and_21_out, not_88_out, not_89_out, not_90_out, not_91_out, not_92_out, not_93_out, not_94_out, not_95_out, not_96_out);
  and and_22 (and_22_out, not_97_out, not_98_out, not_99_out, not_100_out, not_101_out, not_102_out, not_103_out, not_104_out, not_105_out, F5);
  and and_23 (and_23_out, not_106_out, not_107_out, not_108_out, not_109_out, not_110_out, not_111_out, F2, not_112_out, not_113_out, F5);
  and and_24 (and_24_out, not_114_out, not_115_out, not_116_out, not_117_out, not_118_out, not_119_out, F1, not_120_out, not_121_out, not_122_out, not_123_out);
  and and_25 (and_25_out, not_124_out, not_125_out, not_126_out, not_127_out, not_128_out, not_129_out, F1, not_130_out, F3, not_131_out, F5);
  and and_26 (BEQ, not_132_out, not_133_out, OP2, not_134_out, not_135_out, not_136_out);
  and and_27 (BNE, OP0, not_137_out, OP2, not_138_out, not_139_out, not_140_out);
  and and_28 (JR, not_141_out, not_142_out, not_143_out, not_144_out, not_145_out, not_146_out, not_147_out, not_148_out, not_149_out, F3, not_150_out, not_151_out);
  and and_29 (JUMP, not_152_out, OP1, not_153_out, not_154_out, not_155_out, not_156_out);
  and and_30 (JAL, OP0, OP1, not_157_out, not_158_out, not_159_out, not_160_out);
  or or_2 (ALU_SRC, and_3_out, and_4_out, and_5_out, and_6_out);
  or or_3 (RegWrite, and_7_out, and_8_out, and_9_out, and_10_out, and_11_out, and_12_out, and_13_out, and_14_out, and_15_out, and_16_out);
  or or_4 (RegDst, and_21_out, and_22_out, and_23_out, and_24_out, and_25_out);
endmodule

// 新增控制信号生成
module \新增控制信号自动生成  (
  input  OP0,
  input  OP1,
  input  OP2,
  input  OP3,
  input  OP4,
  input  OP5,
  input  F0,
  input  F1,
  input  F2,
  input  F3,
  input  F4,
  input  F5,
  output BLTZ,
  output LH,
  output LUI,
  output SRLV,
  output SET_IE,
  output Clear_IR
);

  wire not_1_out, not_2_out, not_3_out, not_4_out, not_5_out, not_6_out, not_7_out, not_8_out, not_9_out,
       not_10_out, not_11_out, not_12_out, not_13_out, not_14_out, not_15_out, not_16_out, not_17_out,
       not_18_out, not_19_out, not_20_out, not_21_out, not_22_out, not_23_out, not_24_out, not_25_out,
       not_26_out, not_27_out, not_28_out, not_29_out, not_30_out, not_31_out, not_32_out, not_33_out,
       not_34_out, not_35_out, not_36_out, not_37_out, not_38_out, not_39_out;

  not not_1 (not_1_out, OP1);
  not not_2 (not_2_out, OP2);
  not not_3 (not_3_out, OP3);
  not not_4 (not_4_out, OP4);
  not not_5 (not_5_out, OP5);
  not not_6 (not_6_out, OP1);
  not not_7 (not_7_out, OP2);
  not not_8 (not_8_out, OP3);
  not not_9 (not_9_out, OP4);
  not not_10 (not_10_out, OP4);
  not not_11 (not_11_out, OP5);
  not not_12 (not_12_out, OP0);
  not not_13 (not_13_out, OP1);
  not not_14 (not_14_out, OP2);
  not not_15 (not_15_out, OP3);
  not not_16 (not_16_out, OP4);
  not not_17 (not_17_out, OP5);
  not not_18 (not_18_out, F0);
  not not_19 (not_19_out, F3);
  not not_20 (not_20_out, F4);
  not not_21 (not_21_out, F5);
  not not_22 (not_22_out, OP0);
  not not_23 (not_23_out, OP1);
  not not_24 (not_24_out, OP2);
  not not_25 (not_25_out, OP3);
  not not_26 (not_26_out, OP5);
  not not_27 (not_27_out, F0);
  not not_28 (not_28_out, F1);
  not not_29 (not_29_out, F2);
  not not_30 (not_30_out, F5);
  not not_31 (not_31_out, OP0);
  not not_32 (not_32_out, OP1);
  not not_33 (not_33_out, OP2);
  not not_34 (not_34_out, OP3);
  not not_35 (not_35_out, OP5);
  not not_36 (not_36_out, F0);
  not not_37 (not_37_out, F1);
  not not_38 (not_38_out, F2);
  not not_39 (not_39_out, F5);
  and and_1 (BLTZ, OP0, not_1_out, not_2_out, not_3_out, not_4_out, not_5_out);
  and and_2 (LH, OP0, not_6_out, not_7_out, not_8_out, not_9_out, OP5);
  and and_3 (LUI, OP0, OP1, OP2, OP3, not_10_out, not_11_out);
  and and_4 (SRLV, not_12_out, not_13_out, not_14_out, not_15_out, not_16_out, not_17_out, not_18_out, F2, not_19_out, not_20_out, not_21_out);
  and and_5 (SET_IE, not_22_out, not_23_out, not_24_out, not_25_out, OP4, not_26_out, not_27_out, not_28_out, not_29_out, F3, F4, not_30_out);
  and and_6 (Clear_IR, not_31_out, not_32_out, not_33_out, not_34_out, OP4, not_35_out, not_36_out, not_37_out, not_38_out, F3, F4, not_39_out);
endmodule

// ALU
module ALU (
  input  [31:0] X,
  input  [31:0] Y,
  input  [3:0] AluOP,
  output out_4,
  output Equal,
  output out_6,
  output [31:0] Result,
  output [31:0] Result_2
);

  wire [0:0] comparator_1_lt, comparator_2_lt;
  wire [31:0] adder_1_out, AND_out, divider_1_out, divider_1_rem, multiplier_1_cout, multiplier_1_out,
       NOR_out, OR_out, shifter_1_out, shifter_2_out, shifter_3_out, subtractor_1_out, XOR_out;

  assign AND_out = X & Y;  // AND_Gate AND, 32 bits wide
  assign OR_out = X | Y;  // OR_Gate OR, 32 bits wide
  Shifter #(.width(32), .shift("ll")) shifter_1 (.in(X), .\dist (Y[4:0]), .out(shifter_1_out));
  Shifter #(.width(32), .shift("ar")) shifter_2 (.in(X), .\dist (Y[4:0]), .out(shifter_2_out));
  Shifter #(.width(32), .shift("lr")) shifter_3 (.in(X), .\dist (Y[4:0]), .out(shifter_3_out));
  Multiplier #(.width(32)) multiplier_1 (.a(X), .b(Y), .out(multiplier_1_out), .cout(multiplier_1_cout));  // open: cin
  Divider #(.width(32)) divider_1 (.a(X), .b(Y), .out(divider_1_out), .rem(divider_1_rem));  // open: upper
  Adder #(.width(32)) adder_1 (.a(X), .b(Y), .out(adder_1_out));  // open: cin, cout
  Subtractor #(.width(32)) subtractor_1 (.a(X), .b(Y), .out(subtractor_1_out));  // open: bin, bout
  assign XOR_out = X ^ Y;  // XOR_Gate XOR, 32 bits wide
  assign NOR_out = ~(X | Y);  // NOR_Gate NOR, 32 bits wide
  Comparator #(.width(32), .mode("twosComplement")) comparator_1 (
    .a(X), .b(Y), .eq(Equal), .lt(comparator_1_lt[0]));  // open: gt
  Comparator #(.width(32), .mode("unsigned")) comparator_2 (.a(X), .b(Y), .lt(comparator_2_lt[0]));  // open: gt, eq
  Multiplexer #(.select(4), .width(32), .disabled("Z"), .enable("false")) multiplexer_1 (
    .in0(shifter_1_out), .in1(shifter_2_out), .in2(shifter_3_out), .in3(multiplier_1_out),
    .in4(divider_1_out), .in5(adder_1_out), .in6(subtractor_1_out), .in7(AND_out), .in8(OR_out),
    .in9(XOR_out), .in10(NOR_out), .in11({{31{1'b0}}, comparator_1_lt[0]}),
    .in12({{31{1'b0}}, comparator_2_lt[0]}), .in13({32{1'b0}}), .in14({32{1'b0}}), .in15({32{1'b0}}),
    .out(Result), .sel(AluOP));
  Multiplexer #(.select(4), .width(32), .disabled("Z"), .enable("false")) multiplexer_2 (
    .in0({32{1'b0}}), .in1({32{1'b0}}), .in2({32{1'b0}}), .in3(multiplier_1_cout), .in4(divider_1_rem),
    .in5({32{1'b0}}), .in6({32{1'b0}}), .in7({32{1'b0}}), .in8({32{1'b0}}), .in9({32{1'b0}}),
    .in10({32{1'b0}}), .in11({32{1'b0}}), .in12({32{1'b0}}), .in13({32{1'b0}}), .in14({32{1'b0}}),
    .in15({32{1'b0}}), .out(Result_2), .sel(AluOP));
  Multiplexer #(.select(4), .width(1), .disabled("Z"), .enable("false")) multiplexer_3 (
    .in0(1'b0), .in1(1'b0), .in2(1'b0), .in3(1'b0), .in4(1'b0), .in5(1'b0), .in6(1'b0), .in7(1'b0),
    .in8(1'b0), .in9(1'b0), .in10(1'b0), .in11(comparator_1_lt[0]), .in12(comparator_2_lt[0]), .in13(1'b0),
    .in14(1'b0), .in15(1'b0), .out(out_6), .sel(AluOP));
  not not_1 (out_4, out_6);

  // Other names for the same wires on the sheet: Result2[31:0] = Result_2; S[3:0] = AluOP; tunnel = out_6;
  //   tunnel_t = out_4

  // Notes on the sheet:
  //   不要改变此引脚区域内容，也不要改变ALU封装形式
  //   输入引脚
  //   输出引脚
endmodule

module Regifile (
  input  [31:0] Din,
  input  Clk,
  input  WE,
  input  [4:0] R1_num,
  input  [4:0] W_num,
  input  [4:0] R2_num,
  output [31:0] R1,
  output [31:0] R2
);

  // RegisterFile registerfile_1: pin names not known; wires that end beside it: Din, Clk, WE, W_num, R1_num, R2_num, R1, R2
endmodule

module \中断按键参考电路  (
  input  \同步清零信号 ,
  output \与中断屏蔽位与 
);

  wire \_1号中断_out , and_1_out, clock_1_out, d_ff_1_q, or_1_out, or_2_out;

  Clock #(.highDuration(1), .lowDuration(1)) clock_1 (.out(clock_1_out));
  Button \_1号中断  (.out(\_1号中断_out ));
  LED #(.active("true")) \_1号中断等待指示灯  (.in(or_1_out));
  or or_1 (or_1_out, \与中断屏蔽位与 , d_ff_1_q);
  D_Flip_Flop #(.trigger("rising"), .Pre_Clr_Positions("LEGACY"), .NegatePresetClear("false"), .enable("true"), .NewFFLayout("false")) d_ff_1 (
    .clk(\_1号中断_out ), .D(1'b1), .Q(d_ff_1_q), .reset(\与中断屏蔽位与 ));  // open: Qn, preset, en
  or or_2 (or_2_out, d_ff_1_q, \与中断屏蔽位与 );
  and and_1 (and_1_out, or_2_out, ~\同步清零信号 );  // AND_Gate
  D_Flip_Flop #(.trigger("rising"), .Pre_Clr_Positions("LEGACY"), .NegatePresetClear("false"), .enable("true"), .NewFFLayout("false")) IR1 (
    .clk(clock_1_out), .D(and_1_out), .Q(\与中断屏蔽位与 ));  // open: Qn, preset, en, reset

  // Notes on the sheet:
  //   中断信号采样参考电路
  //   Reset 
endmodule

module \单周期_单级中断  (
  input  IR1,
  input  IR2,
  input  IR3,
  output RegWrite,
  output MemWrite,
  output [31:0] PC,
  output [31:0] IR,
  output [31:0] RDin,
  output [31:0] MDin,
  output [31:0] LedData
);

  wire ALUeq, ALUge, ALUle, and_1_out, and_2_out, and_3_out, and_4_out, and_6_out, and_7_out, and_8_out,
       and_9_out, and_10_out, Beq, BGEU, Bne, Btype, CLK, clock_1_out, CLR1, CLR2, CLR3, comparator_1_eq,
       comparator_2_eq, comparator_3_eq, comparator_4_eq, comparator_5_eq, comparator_5_lt, comparator_6_eq,
       comparator_6_gt, comparator_6_lt, comparator_7_eq, d_ff_1_q, d_ff_2_q, d_ff_3_q, d_ff_4_q, ecall, Go,
       halt, halt_1, IE, INTR, INTR1, INTR2, INTR3, IR1_t, IR2_t, IR3_t, IRA, IRB, IRC, IRHAVE, JAL, JALR,
       Jtype, LHU, LUI, MemToReg, nand_1_out, not_1_out, not_2_out, not_3_out, or_1_out, or_7_out, or_9_out,
       or_12_out, or_13_out, or_14_out, or_16_out, or_17_out, RST, SRA, Stype, URET, W1, W2, W3,
       \单周期硬布线控制器_1_p17 ;
  wire [1:0] priority_encoder_1_out, priority_encoder_2_out, priority_encoder_3_out, register_1_q;
  wire [3:0] \单周期硬布线控制器_1_p16 ;
  wire [4:0] multiplexer_4_out, multiplexer_5_out;
  wire [12:0] CNT_num;
  wire [15:0] multiplexer_9_out, \总周期数 ;
  wire [31:0] ALUres, bit_extender_1_out, bit_extender_2_out, bit_extender_3_out, bit_extender_4_out,
       bit_extender_5_out, bit_extender_6_out, Dout, IR_PC, MEPC, multiplexer_2_out, multiplexer_3_out,
       multiplexer_6_out, multiplexer_7_out, multiplexer_8_out, multiplexer_10_out, PC_4, PC_B, PC_J,
       regifile_1_r1, shifter_1_out, shifter_2_out, shifter_3_out;

  Button \u_继续运行  (.out(Go));
  Button _1 (.out(IRA));
  Button _2 (.out(IRB));
  Button _3 (.out(IRC));
  LED #(.active("true")) led_1 (.in(W1));
  LED #(.active("true")) led_2 (.in(W2));
  LED #(.active("true")) led_3 (.in(W3));
  Hex_Digit_Display hex_digit_display_1 (.value(LedData[31:28]));  // open: dp
  Comparator #(.width(16), .mode("twosComplement")) comparator_1 (
    .a(16'h23b), .b(\总周期数 ), .eq(comparator_1_eq));  // open: gt, lt
  Comparator #(.width(16), .mode("twosComplement")) comparator_2 (
    .a(\总周期数 ), .b(16'h1), .eq(comparator_2_eq));  // open: gt, lt
  Comparator #(.width(16), .mode("twosComplement")) comparator_3 (
    .a(\总周期数 ), .b(16'h4), .eq(comparator_3_eq));  // open: gt, lt
  Comparator #(.width(16), .mode("twosComplement")) comparator_4 (
    .a(\总周期数 ), .b(16'h7), .eq(comparator_4_eq));  // open: gt, lt
  not not_1 (not_1_out, ALUeq);
  Hex_Digit_Display hex_digit_display_2 (.value(LedData[27:24]));  // open: dp
  Hex_Digit_Display hex_digit_display_3 (.value(LedData[23:20]));  // open: dp
  or or_1 (or_1_out, comparator_1_eq, comparator_2_eq);
  assign IRA = or_1_out ? ~CLK : 1'bz;  // Controlled_Inverter controlled_inverter_1
  assign IRB = comparator_3_eq ? ~CLK : 1'bz;  // Controlled_Inverter controlled_inverter_2
  assign IRC = comparator_4_eq ? ~CLK : 1'bz;  // Controlled_Inverter controlled_inverter_3
  and and_1 (and_1_out, Beq, ALUeq);
  and and_2 (and_2_out, not_1_out, Bne);
  and and_3 (and_3_out, BGEU, ALUge);
  Multiplexer #(.select(2), .width(32), .disabled("Z"), .enable("false")) multiplexer_1 (
    .in0(32'h30ac), .in1(32'h3150), .in2(32'h31f4), .out(IR_PC), .sel(priority_encoder_1_out));  // open: in3
  Priority_Encoder #(.select(2), .disabled("Z")) priority_encoder_1 (
    .in0(INTR1), .in1(INTR2), .in2(INTR3), .out(priority_encoder_1_out));  // open: in3, gs, en_out, en_in
  Hex_Digit_Display hex_digit_display_4 (.value(LedData[15:12]));  // open: dp
  Hex_Digit_Display hex_digit_display_5 (.value(LedData[19:16]));  // open: dp
  Pull_Resistor #(.pull(0)) pull_resistor_1 (.node(IRA));
  Pull_Resistor #(.pull(0)) pull_resistor_2 (.node(IRB));
  Pull_Resistor #(.pull(0)) pull_resistor_3 (.node(IRC));
  or or_2 (Btype, and_1_out, and_2_out, and_3_out);
  Hex_Digit_Display hex_digit_display_6 (.value(LedData[11:8]));  // open: dp
  Hex_Digit_Display hex_digit_display_7 (.value(LedData[7:4]));  // open: dp
  // Probe on \总周期数 
  Hex_Digit_Display hex_digit_display_8 (.value(LedData[3:0]));  // open: dp
  Priority_Encoder #(.select(2), .disabled("Z")) priority_encoder_2 (
    .in0(1'b1), .in1(JALR), .in2(JAL), .in3(Btype), .out(priority_encoder_2_out));  // open: gs, en_out, en_in
  Multiplexer #(.select(2), .width(32), .disabled("Z"), .enable("false")) multiplexer_2 (
    .in0(PC_4), .in1(ALUres), .in2(PC_J), .in3(PC_B), .out(multiplexer_2_out), .sel(priority_encoder_2_out));
  or or_3 (W1, INTR1, d_ff_1_q);
  Register #(.width(2), .trigger("rising"), .Select("low")) register_1 (
    .D(priority_encoder_1_out), .en(INTR), .Q(register_1_q), .clk(CLK));  // open: clr
  Demultiplexer #(.select(2), .width(1), .tristate("false"), .disabled("Z"), .enable("false")) demultiplexer_1 (
    .out0(CLR1), .out1(CLR2), .out2(CLR3), .in(URET), .sel(register_1_q));  // open: out3
  or or_4 (IR1_t, IR1, IRA);
  D_Flip_Flop #(.trigger("rising"), .Pre_Clr_Positions("LEGACY"), .NegatePresetClear("false"), .enable("true"), .NewFFLayout("false")) d_ff_1 (
    .clk(IRA), .D(1'b1), .Q(d_ff_1_q), .reset(INTR1));  // open: Qn, preset, en
  or or_5 (IR2_t, IR2, IRB);
  or or_6 (IRHAVE, INTR1, INTR2, INTR3);
  Multiplexer #(.select(2), .width(32), .disabled("Z"), .enable("false")) multiplexer_3 (
    .in0(multiplexer_2_out), .in1(IR_PC), .in2(MEPC), .out(multiplexer_3_out), .sel(priority_encoder_3_out));  // open: in3
  Priority_Encoder #(.select(2), .disabled("Z")) priority_encoder_3 (
    .in0(1'b1), .in1(INTR), .in2(URET), .out(priority_encoder_3_out));  // open: in3, gs, en_out, en_in
  or or_7 (or_7_out, d_ff_1_q, INTR1);
  and and_4 (and_4_out, or_7_out, ~CLR1);  // AND_Gate
  Register #(.width(32), .trigger("rising"), .Select("low")) register_2 (
    .D(multiplexer_2_out), .en(INTR), .Q(MEPC), .clk(CLK));  // open: clr
  or or_8 (IR3_t, IR3, IRC);
  and and_5 (INTR, IE, IRHAVE);
  D_Flip_Flop #(.trigger("rising"), .Pre_Clr_Positions("LEGACY"), .NegatePresetClear("false"), .enable("true"), .NewFFLayout("false")) u_IR1 (
    .clk(CLK), .D(and_4_out), .Q(INTR1));  // open: Qn, preset, en, reset
  Register #(.width(32), .trigger("rising"), .Select("low")) u_PC (
    .D(multiplexer_3_out), .en(or_9_out), .Q(PC), .clk(CLK), .clr(RST));
  or or_9 (or_9_out, Go, not_2_out);
  not not_2 (not_2_out, halt);
  or or_10 (Jtype, JAL, JALR);
  // RiscV_Probe riscv_probe_1: pin names not known; wires that end beside it: IR
  Adder #(.width(32)) adder_1 (.a(PC), .b(32'h4), .out(PC_4));  // open: cin, cout
  or or_11 (W2, INTR2, d_ff_2_q);
  ROM #(.addrWidth(10), .dataWidth(32), .Select("high")) rom_1 (.addr(PC[11:2]), .data(IR));
  not not_3 (not_3_out, halt);
  D_Flip_Flop #(.trigger("rising"), .Pre_Clr_Positions("LEGACY"), .NegatePresetClear("false"), .enable("true"), .NewFFLayout("false")) d_ff_2 (
    .clk(IRB), .D(1'b1), .Q(d_ff_2_q), .reset(INTR2));  // open: Qn, preset, en
  or or_12 (or_12_out, Go, not_3_out);
  // 单周期硬布线控制器 单周期硬布线控制器_1: pin names not known; wires that end beside it: JAL, SRA, JALR, LUI, URET, IR[21], IR[6:2], {IR[30], IR[25], IR[14:12]}, LHU, ecall, BGEU, Beq, Bne, MemToReg, MemWrite, \单周期硬布线控制器_1_p16 , \单周期硬布线控制器_1_p17 , RegWrite, Stype
  Multiplexer #(.select(1), .width(5), .disabled("Z"), .enable("false")) multiplexer_4 (
    .in0(IR[19:15]), .in1(5'b10001), .out(multiplexer_4_out), .sel(ecall));
  Multiplexer #(.select(1), .width(5), .disabled("Z"), .enable("false")) multiplexer_5 (
    .in0(IR[24:20]), .in1(5'b01010), .out(multiplexer_5_out), .sel(ecall));
  Counter #(.width(16), .max('hffff), .ongoal("wrap"), .trigger("rising"), .behavior("new")) counter_1 (
    .count(or_12_out), .Q(\总周期数 ), .clk(CLK));  // open: load, D, carry, clr, preset, down
  or or_13 (or_13_out, d_ff_2_q, INTR2);
  and and_6 (and_6_out, or_13_out, ~CLR2);  // AND_Gate
  assign bit_extender_1_out = {{20{IR[31]}}, IR[31:20]};  // Bit_Extender bit_extender_1
  Multiplexer #(.select(1), .width(32), .disabled("Z"), .enable("false")) multiplexer_6 (
    .in0(bit_extender_1_out), .in1(bit_extender_2_out), .out(multiplexer_6_out), .sel(Stype));
  assign bit_extender_2_out = {{20{IR[31]}}, {IR[31:25], IR[11:7]}};  // Bit_Extender bit_extender_2
  assign bit_extender_3_out = {{20{IR[31]}}, {IR[31], IR[7], IR[30:25], IR[11:8]}};  // Bit_Extender bit_extender_3
  assign bit_extender_4_out = {{12{IR[31]}}, {IR[31], IR[19:12], IR[20], IR[30:21]}};  // Bit_Extender bit_extender_4
  D_Flip_Flop #(.trigger("high"), .Pre_Clr_Positions("LEGACY"), .NegatePresetClear("false"), .enable("true"), .NewFFLayout("false")) d_ff_3 (.Q(d_ff_3_q));  // open: clk, D, Qn, preset, en, reset
  // Probe on 13'hc
  D_Flip_Flop #(.trigger("rising"), .Pre_Clr_Positions("LEGACY"), .NegatePresetClear("false"), .enable("true"), .NewFFLayout("false")) u_IR2 (
    .clk(CLK), .D(and_6_out), .Q(INTR2));  // open: Qn, preset, en, reset
  Regifile regifile_1 (
    .Din(RDin), .Clk(CLK), .R1(regifile_1_r1), .R2(MDin), .WE(RegWrite), .W_num(IR[11:7]),
    .R1_num(multiplexer_4_out), .R2_num(multiplexer_5_out));
  Shifter #(.width(32), .shift("ll")) shifter_1 (.in(bit_extender_3_out), .\dist (5'b00001), .out(shifter_1_out));
  Shifter #(.width(32), .shift("ll")) shifter_2 (.in(bit_extender_4_out), .\dist (5'b00001), .out(shifter_2_out));
  Comparator #(.width(13), .mode("twosComplement")) comparator_5 (
    .a(CNT_num), .b(13'hc), .eq(comparator_5_eq), .lt(comparator_5_lt));  // open: gt
  Clock #(.highDuration(1), .lowDuration(1)) clock_1 (.out(clock_1_out));
  Multiplexer #(.select(1), .width(32), .disabled("Z"), .enable("false")) multiplexer_7 (
    .in0(MDin), .in1(multiplexer_6_out), .out(multiplexer_7_out), .sel(\单周期硬布线控制器_1_p17 ));
  Counter #(.width(13), .max('h1fff), .ongoal("stay"), .trigger("rising"), .behavior("old")) counter_2 (
    .count(comparator_5_lt), .Q(CNT_num), .clk(clock_1_out));  // open: load, D, carry, clr, preset
  Adder #(.width(32)) adder_2 (.a(shifter_1_out), .b(PC), .out(PC_B));  // open: cin, cout
  Adder #(.width(32)) adder_3 (.a(shifter_2_out), .b(PC), .out(PC_J));  // open: cin, cout
  nand nand_1 (nand_1_out, d_ff_3_q, comparator_5_eq);
  or or_14 (or_14_out, ~IRHAVE, URET);  // OR_Gate
  or or_15 (W3, INTR3, d_ff_4_q);
  Comparator #(.width(32), .mode("twosComplement")) comparator_6 (
    .a(32'h22), .b(regifile_1_r1), .gt(comparator_6_gt), .eq(comparator_6_eq), .lt(comparator_6_lt));
  ALU alu_1 (
    .X(regifile_1_r1), .Y(multiplexer_7_out), .AluOP(\单周期硬布线控制器_1_p16 ), .Equal(ALUeq), .Result(ALUres),
    .out_4(ALUge), .out_6(ALUle));  // open: Result_2
  assign CLK = nand_1_out ? clock_1_out : 1'bz;  // Controlled_Buffer controlled_buffer_1
  Pull_Resistor #(.pull(1)) pull_resistor_4 (.node(CLK));
  D_Flip_Flop #(.trigger("rising"), .Pre_Clr_Positions("LEGACY"), .NegatePresetClear("false"), .enable("true"), .NewFFLayout("false")) d_ff_4 (
    .clk(IRC), .D(1'b1), .Q(d_ff_4_q), .reset(INTR3));  // open: Qn, preset, en
  and and_7 (and_7_out, ecall, comparator_6_eq);
  D_Flip_Flop #(.trigger("rising"), .Pre_Clr_Positions("LEGACY"), .NegatePresetClear("false"), .enable("true"), .NewFFLayout("true")) d_ff_5 (
    .clk(CLK), .D(or_14_out), .Q(IE));  // open: Qn, preset, en, reset
  Register #(.width(32), .trigger("rising"), .Select("low")) register_3 (
    .D(MDin), .en(and_7_out), .Q(LedData), .clk(CLK));  // open: clr
  or or_16 (or_16_out, d_ff_4_q, INTR3);
  and and_8 (and_8_out, or_16_out, ~CLR3);  // AND_Gate
  and and_9 (and_9_out, or_17_out, ecall);
  or or_17 (or_17_out, comparator_6_gt, comparator_6_lt);
  Multiplexer #(.select(2), .width(32), .disabled("Z"), .enable("false")) multiplexer_8 (
    .in0(ALUres), .in1(Dout), .in2(PC_4), .in3(PC_4), .out(multiplexer_8_out), .sel({Jtype, MemToReg}));
  D_Flip_Flop #(.trigger("rising"), .Pre_Clr_Positions("LEGACY"), .NegatePresetClear("false"), .enable("true"), .NewFFLayout("false")) u_IR3 (
    .clk(CLK), .D(and_8_out), .Q(INTR3));  // open: Qn, preset, en, reset
  D_Flip_Flop #(.trigger("falling"), .Pre_Clr_Positions("ABOVE_BELOW"), .NegatePresetClear("false"), .enable("true"), .NewFFLayout("true")) d_ff_6 (
    .clk(CLK), .D(1'b1), .Q(halt_1), .en(and_9_out), .reset(Go));  // open: Qn, preset
  RAM #(.addrWidth(10), .dataWidth(32), .bus("separate"), .Select("high")) ram_1 (
    .addr(ALUres[11:2]), .din(MDin), .data(Dout), .str(MemWrite), .sel(1'b1), .clk(CLK), .ld(1'b1));  // open: clr
  Comparator #(.width(32), .mode("twosComplement")) comparator_7 (
    .a(32'h1), .b(LedData), .eq(comparator_7_eq));  // open: gt, lt
  and and_10 (and_10_out, BGEU, comparator_7_eq);
  Multiplexer #(.select(1), .width(16), .disabled("Z"), .enable("false")) multiplexer_9 (
    .in0(multiplexer_8_out[15:0]), .in1(multiplexer_8_out[31:16]), .out(multiplexer_9_out), .sel(ALUres[0]));
  or or_18 (halt, and_10_out, halt_1);
  assign bit_extender_5_out = {{16{1'b0}}, multiplexer_9_out};  // Bit_Extender bit_extender_5
  assign bit_extender_6_out = {{12{1'b0}}, IR[31:12]};  // Bit_Extender bit_extender_6
  Multiplexer #(.select(1), .width(32), .disabled("Z"), .enable("false")) multiplexer_10 (
    .in0(multiplexer_8_out), .in1(bit_extender_5_out), .out(multiplexer_10_out), .sel(LHU));
  Shifter #(.width(32), .shift("ll")) shifter_3 (.in(bit_extender_6_out), .\dist (5'b01100), .out(shifter_3_out));
  Multiplexer #(.select(1), .width(32), .disabled("Z"), .enable("false")) multiplexer_11 (
    .in0(multiplexer_10_out), .in1(shifter_3_out), .out(RDin), .sel(LUI));

  // Other names for the same wires on the sheet: Imm[19:0] = IR[31:12]

  // Notes on the sheet:
  //   中断源
  //   中断等待指示
  //   总复位信号应将除ROM以外所有存储组件全部清零
  //   单级中断测试信号模拟器
  //   数码管输出
  //   数码管输出应该用寄存器锁存，否则显示数据只能一闪而过
  //   中断响应阶段
  //   中断响应
  //   指令探针
  //   指令存储器
  //   为方便自动评测，需要输出PC，IR，寄存器堆写如数据RDin
  //   指令字
  //   contents of rom_1 (hex, n*v repeats v):
  //   7d000113 100413 1f41993 41f9d993 433 c00913 800b13 140413 f47413 800293 100313 499993 89e9b3 1300533
  //   2200893 73 406282b3 fe0294e3 140413 f00f93 1f47433 1c41413 800293 100313 49d993 89e9b3 1300533
  //   2200893 73 406282b3 fe0294e3 1c45413 406b0b33 b0463 f95ff06f 2b3 fff2c293 1029293 fff2e293 500533
  //   2200893 73 f5dff06f 1112023 410113 a12023 410113 812023 410113 1312023 410113 1412023 410113 1512023
  //   410113 1612023 410113 100b13 300a13 100a93 1600433 441413 14469b3 1300533 2200893 73 fe0416e3
  //   415a0a33 fe0a10e3 ffc10113 12b03 ffc10113 12a83 ffc10113 12a03 ffc10113 12983 ffc10113 12403
  //   ffc10113 12503 ffc10113 12883 200073 1112023 410113 a12023 410113 812023 410113 1312023 410113
  //   1412023 410113 1512023 410113 1612023 410113 200b13 300a13 100a93 1600433 441413 14469b3 1300533
  //   2200893 73 fe0416e3 415a0a33 fe0a10e3 ffc10113 12b03 ffc10113 12a83 ffc10113 12a03 ffc10113 12983
  //   ffc10113 12403 ffc10113 12503 ffc10113 12883 200073 1112023 410113 a12023 410113 812023 410113
  //   1312023 410113 1412023 410113 1512023 410113 1612023 410113 300b13 300a13 100a93 1600433 441413
  //   14469b3 1300533 2200893 73 fe0416e3 415a0a33 fe0a10e3 ffc10113 12b03 ffc10113 12a83 ffc10113 12a03
  //   ffc10113 12983 ffc10113 12403 ffc10113 12503 ffc10113 12883 200073
  //   RAM写使能MemWrite、RAM写入数据MDin等信号
  //   JALR
  //   URET
  //   Beq
  //   Bne
  //   MemToReg
  //   MemWrite
  //   AluOP
  //   AluSrcB
  //   RegWrite
  //   控制位
  //   暂停节拍，不能为0
  //   戳工具置1进入计数暂停模式，ctrl+k时钟自动运行到对应节拍暂停
  //   ctrl+k关闭时钟连续运行，将控制位置零，进入单步调试模式调试
  //   中断使能位(用于开关中断)
  //   判断中断使能
  //   可计数暂停的时钟源
  //   数据存储器
endmodule

module MapReg_1 (
  input  [31:0] Data,
  input  En,
  input  [9:0] Addr,
  input  CLK,
  input  RST,
  output [31:0] \行1 ,
  output [31:0] \行9 ,
  output [31:0] \行17 ,
  output [31:0] \行25 ,
  output [31:0] \行2 ,
  output [31:0] \行10 ,
  output [31:0] \行18 ,
  output [31:0] \行26 ,
  output [31:0] \行3 ,
  output [31:0] \行11 ,
  output [31:0] \行19 ,
  output [31:0] \行27 ,
  output [31:0] \行4 ,
  output [31:0] \行12 ,
  output [31:0] \行20 ,
  output [31:0] \行28 ,
  output [31:0] \行5 ,
  output [31:0] \行13 ,
  output [31:0] \行21 ,
  output [31:0] \行29 ,
  output [31:0] \行6 ,
  output [31:0] \行14 ,
  output [31:0] \行22 ,
  output [31:0] \行30 ,
  output [31:0] \行7 ,
  output [31:0] \行15 ,
  output [31:0] \行23 ,
  output [31:0] \行31 ,
  output [31:0] \行8 ,
  output [31:0] \行16 ,
  output [31:0] \行24 ,
  output [31:0] \行32 
);

  wire and_1_out, and_2_out, and_3_out, and_4_out, and_5_out, and_6_out, and_7_out, and_8_out, and_9_out,
       and_10_out, and_11_out, and_12_out, and_13_out, and_14_out, and_15_out, and_16_out, and_17_out,
       and_18_out, and_19_out, and_20_out, and_21_out, and_22_out, and_23_out, and_24_out, and_25_out,
       and_26_out, and_27_out, and_28_out, and_29_out, and_30_out, and_31_out, and_32_out, \行1_t , \行2_t ,
       \行3_t , \行4_t , \行5_t , \行6_t , \行7_t , \行8_t , \行9_t , \行10_t , \行11_t , \行12_t , \行13_t , \行14_t ,
       \行15_t , \行16_t , \行17_t , \行18_t , \行19_t , \行20_t , \行21_t , \行22_t , \行23_t , \行24_t , \行25_t ,
       \行26_t , \行27_t , \行28_t , \行29_t , \行30_t , \行31_t , \行32_t ;

  and and_1 (and_1_out, En, \行1_t );
  and and_2 (and_2_out, En, \行2_t );
  and and_3 (and_3_out, En, \行3_t );
  and and_4 (and_4_out, En, \行4_t );
  and and_5 (and_5_out, En, \行5_t );
  and and_6 (and_6_out, En, \行6_t );
  and and_7 (and_7_out, En, \行7_t );
  and and_8 (and_8_out, En, \行8_t );
  Register #(.width(32), .trigger("rising"), .Select("low")) register_1 (
    .D(Data), .en(and_1_out), .Q(\行1 ), .clk(CLK), .clr(RST));
  Register #(.width(32), .trigger("rising"), .Select("low")) register_2 (
    .D(Data), .en(and_2_out), .Q(\行2 ), .clk(CLK), .clr(RST));
  Register #(.width(32), .trigger("rising"), .Select("low")) register_3 (
    .D(Data), .en(and_3_out), .Q(\行3 ), .clk(CLK), .clr(RST));
  Register #(.width(32), .trigger("rising"), .Select("low")) register_4 (
    .D(Data), .en(and_4_out), .Q(\行4 ), .clk(CLK), .clr(RST));
  Register #(.width(32), .trigger("rising"), .Select("low")) register_5 (
    .D(Data), .en(and_5_out), .Q(\行5 ), .clk(CLK), .clr(RST));
  Register #(.width(32), .trigger("rising"), .Select("low")) register_6 (
    .D(Data), .en(and_6_out), .Q(\行6 ), .clk(CLK), .clr(RST));
  Register #(.width(32), .trigger("rising"), .Select("low")) register_7 (
    .D(Data), .en(and_7_out), .Q(\行7 ), .clk(CLK), .clr(RST));
  Register #(.width(32), .trigger("rising"), .Select("low")) register_8 (
    .D(Data), .en(and_8_out), .Q(\行8 ), .clk(CLK), .clr(RST));
  and and_9 (and_9_out, En, \行9_t );
  and and_10 (and_10_out, En, \行10_t );
  and and_11 (and_11_out, En, \行11_t );
  and and_12 (and_12_out, En, \行12_t );
  and and_13 (and_13_out, En, \行13_t );
  and and_14 (and_14_out, En, \行14_t );
  and and_15 (and_15_out, En, \行15_t );
  and and_16 (and_16_out, En, \行16_t );
  Register #(.width(32), .trigger("rising"), .Select("low")) register_9 (
    .D(Data), .en(and_9_out), .Q(\行9 ), .clk(CLK), .clr(RST));
  Register #(.width(32), .trigger("rising"), .Select("low")) register_10 (
    .D(Data), .en(and_10_out), .Q(\行10 ), .clk(CLK), .clr(RST));
  Register #(.width(32), .trigger("rising"), .Select("low")) register_11 (
    .D(Data), .en(and_11_out), .Q(\行11 ), .clk(CLK), .clr(RST));
  Register #(.width(32), .trigger("rising"), .Select("low")) register_12 (
    .D(Data), .en(and_12_out), .Q(\行12 ), .clk(CLK), .clr(RST));
  Register #(.width(32), .trigger("rising"), .Select("low")) register_13 (
    .D(Data), .en(and_13_out), .Q(\行13 ), .clk(CLK), .clr(RST));
  Register #(.width(32), .trigger("rising"), .Select("low")) register_14 (
    .D(Data), .en(and_14_out), .Q(\行14 ), .clk(CLK), .clr(RST));
  Register #(.width(32), .trigger("rising"), .Select("low")) register_15 (
    .D(Data), .en(and_15_out), .Q(\行15 ), .clk(CLK), .clr(RST));
  Register #(.width(32), .trigger("rising"), .Select("low")) register_16 (
    .D(Data), .en(and_16_out), .Q(\行16 ), .clk(CLK), .clr(RST));
  and and_17 (and_17_out, En, \行17_t );
  and and_18 (and_18_out, En, \行18_t );
  and and_19 (and_19_out, En, \行19_t );
  and and_20 (and_20_out, En, \行20_t );
  and and_21 (and_21_out, En, \行21_t );
  and and_22 (and_22_out, En, \行22_t );
  and and_23 (and_23_out, En, \行23_t );
  and and_24 (and_24_out, En, \行24_t );
  Register #(.width(32), .trigger("rising"), .Select("low")) register_17 (
    .D(Data), .en(and_17_out), .Q(\行17 ), .clk(CLK), .clr(RST));
  Register #(.width(32), .trigger("rising"), .Select("low")) register_18 (
    .D(Data), .en(and_18_out), .Q(\行18 ), .clk(CLK), .clr(RST));
  Register #(.width(32), .trigger("rising"), .Select("low")) register_19 (
    .D(Data), .en(and_19_out), .Q(\行19 ), .clk(CLK), .clr(RST));
  Register #(.width(32), .trigger("rising"), .Select("low")) register_20 (
    .D(Data), .en(and_20_out), .Q(\行20 ), .clk(CLK), .clr(RST));
  Register #(.width(32), .trigger("rising"), .Select("low")) register_21 (
    .D(Data), .en(and_21_out), .Q(\行21 ), .clk(CLK), .clr(RST));
  Register #(.width(32), .trigger("rising"), .Select("low")) register_22 (
    .D(Data), .en(and_22_out), .Q(\行22 ), .clk(CLK), .clr(RST));
  Register #(.width(32), .trigger("rising"), .Select("low")) register_23 (
    .D(Data), .en(and_23_out), .Q(\行23 ), .clk(CLK), .clr(RST));
  Register #(.width(32), .trigger("rising"), .Select("low")) register_24 (
    .D(Data), .en(and_24_out), .Q(\行24 ), .clk(CLK), .clr(RST));
  and and_25 (and_25_out, En, \行25_t );
  and and_26 (and_26_out, En, \行26_t );
  and and_27 (and_27_out, En, \行27_t );
  and and_28 (and_28_out, En, \行28_t );
  and and_29 (and_29_out, En, \行29_t );
  and and_30 (and_30_out, En, \行30_t );
  and and_31 (and_31_out, En, \行31_t );
  and and_32 (and_32_out, En, \行32_t );
  Register #(.width(32), .trigger("rising"), .Select("low")) register_25 (
    .D(Data), .en(and_25_out), .Q(\行25 ), .clk(CLK), .clr(RST));
  Register #(.width(32), .trigger("rising"), .Select("low")) register_26 (
    .D(Data), .en(and_26_out), .Q(\行26 ), .clk(CLK), .clr(RST));
  Register #(.width(32), .trigger("rising"), .Select("low")) register_27 (
    .D(Data), .en(and_27_out), .Q(\行27 ), .clk(CLK), .clr(RST));
  Register #(.width(32), .trigger("rising"), .Select("low")) register_28 (
    .D(Data), .en(and_28_out), .Q(\行28 ), .clk(CLK), .clr(RST));
  Register #(.width(32), .trigger("rising"), .Select("low")) register_29 (
    .D(Data), .en(and_29_out), .Q(\行29 ), .clk(CLK), .clr(RST));
  Register #(.width(32), .trigger("rising"), .Select("low")) register_30 (
    .D(Data), .en(and_30_out), .Q(\行30 ), .clk(CLK), .clr(RST));
  Register #(.width(32), .trigger("rising"), .Select("low")) register_31 (
    .D(Data), .en(and_31_out), .Q(\行31 ), .clk(CLK), .clr(RST));
  Register #(.width(32), .trigger("rising"), .Select("low")) register_32 (
    .D(Data), .en(and_32_out), .Q(\行32 ), .clk(CLK), .clr(RST));
  Demultiplexer #(.select(5), .width(1), .tristate("false"), .disabled("Z"), .enable("false")) demultiplexer_1 (
    .out0(\行1_t ), .out1(\行2_t ), .out2(\行3_t ), .out3(\行4_t ), .out4(\行5_t ), .out5(\行6_t ), .out6(\行7_t ),
    .out7(\行8_t ), .out8(\行9_t ), .out9(\行10_t ), .out10(\行11_t ), .out11(\行12_t ), .out12(\行13_t ),
    .out13(\行14_t ), .out14(\行15_t ), .out15(\行16_t ), .out16(\行17_t ), .out17(\行18_t ), .out18(\行19_t ),
    .out19(\行20_t ), .out20(\行21_t ), .out21(\行22_t ), .out22(\行23_t ), .out23(\行24_t ), .out24(\行25_t ),
    .out25(\行26_t ), .out26(\行27_t ), .out27(\行28_t ), .out28(\行29_t ), .out29(\行30_t ), .out30(\行31_t ),
    .out31(\行32_t ), .in(1'b1), .sel(Addr[4:0]));
endmodule

module MapReg_2 (
  input  En,
  input  [31:0] _1,
  input  [31:0] _9,
  input  [31:0] _17,
  input  [31:0] _25,
  input  [31:0] _2,
  input  [31:0] _10,
  input  [31:0] _18,
  input  [31:0] _26,
  input  [31:0] _3,
  input  [31:0] _11,
  input  [31:0] _19,
  input  [31:0] _27,
  input  [31:0] _4,
  input  [31:0] _12,
  input  [31:0] _20,
  input  [31:0] _28,
  input  [31:0] _5,
  input  [31:0] _13,
  input  [31:0] _21,
  input  [31:0] _29,
  input  [31:0] _6,
  input  [31:0] _14,
  input  [31:0] _22,
  input  [31:0] _30,
  input  [31:0] _7,
  input  [31:0] _15,
  input  [31:0] _23,
  input  [31:0] _31,
  input  [31:0] _8,
  input  [31:0] _16,
  input  [31:0] _24,
  input  [31:0] _32,
  input  CLK,
  input  RST,
  output [31:0] \行1 ,
  output [31:0] \行9 ,
  output [31:0] \行17 ,
  output [31:0] \行25 ,
  output [31:0] \行2 ,
  output [31:0] \行10 ,
  output [31:0] \行18 ,
  output [31:0] \行26 ,
  output [31:0] \行3 ,
  output [31:0] \行11 ,
  output [31:0] \行19 ,
  output [31:0] \行27 ,
  output [31:0] \行4 ,
  output [31:0] \行12 ,
  output [31:0] \行20 ,
  output [31:0] \行28 ,
  output [31:0] \行5 ,
  output [31:0] \行13 ,
  output [31:0] \行21 ,
  output [31:0] \行29 ,
  output [31:0] \行6 ,
  output [31:0] \行14 ,
  output [31:0] \行22 ,
  output [31:0] \行30 ,
  output [31:0] \行7 ,
  output [31:0] \行15 ,
  output [31:0] \行23 ,
  output [31:0] \行31 ,
  output [31:0] \行8 ,
  output [31:0] \行16 ,
  output [31:0] \行24 ,
  output [31:0] \行32 
);

  Register #(.width(32), .trigger("rising"), .Select("low")) register_1 (
    .D(_1), .en(En), .Q(\行1 ), .clk(CLK), .clr(RST));
  Register #(.width(32), .trigger("rising"), .Select("low")) register_2 (
    .D(_2), .en(En), .Q(\行2 ), .clk(CLK), .clr(RST));
  Register #(.width(32), .trigger("rising"), .Select("low")) register_3 (
    .D(_3), .en(En), .Q(\行3 ), .clk(CLK), .clr(RST));
  Register #(.width(32), .trigger("rising"), .Select("low")) register_4 (
    .D(_4), .en(En), .Q(\行4 ), .clk(CLK), .clr(RST));
  Register #(.width(32), .trigger("rising"), .Select("low")) register_5 (
    .D(_5), .en(En), .Q(\行5 ), .clk(CLK), .clr(RST));
  Register #(.width(32), .trigger("rising"), .Select("low")) register_6 (
    .D(_6), .en(En), .Q(\行6 ), .clk(CLK), .clr(RST));
  Register #(.width(32), .trigger("rising"), .Select("low")) register_7 (
    .D(_7), .en(En), .Q(\行7 ), .clk(CLK), .clr(RST));
  Register #(.width(32), .trigger("rising"), .Select("low")) register_8 (
    .D(_8), .en(En), .Q(\行8 ), .clk(CLK), .clr(RST));
  Register #(.width(32), .trigger("rising"), .Select("low")) register_9 (
    .D(_9), .en(En), .Q(\行9 ), .clk(CLK), .clr(RST));
  Register #(.width(32), .trigger("rising"), .Select("low")) register_10 (
    .D(_10), .en(En), .Q(\行10 ), .clk(CLK), .clr(RST));
  Register #(.width(32), .trigger("rising"), .Select("low")) register_11 (
    .D(_11), .en(En), .Q(\行11 ), .clk(CLK), .clr(RST));
  Register #(.width(32), .trigger("rising"), .Select("low")) register_12 (
    .D(_12), .en(En), .Q(\行12 ), .clk(CLK), .clr(RST));
  Register #(.width(32), .trigger("rising"), .Select("low")) register_13 (
    .D(_13), .en(En), .Q(\行13 ), .clk(CLK), .clr(RST));
  Register #(.width(32), .trigger("rising"), .Select("low")) register_14 (
    .D(_14), .en(En), .Q(\行14 ), .clk(CLK), .clr(RST));
  Register #(.width(32), .trigger("rising"), .Select("low")) register_15 (
    .D(_15), .en(En), .Q(\行15 ), .clk(CLK), .clr(RST));
  Register #(.width(32), .trigger("rising"), .Select("low")) register_16 (
    .D(_16), .en(En), .Q(\行16 ), .clk(CLK), .clr(RST));
  Register #(.width(32), .trigger("rising"), .Select("low")) register_17 (
    .D(_17), .en(En), .Q(\行17 ), .clk(CLK), .clr(RST));
  Register #(.width(32), .trigger("rising"), .Select("low")) register_18 (
    .D(_18), .en(En), .Q(\行18 ), .clk(CLK), .clr(RST));
  Register #(.width(32), .trigger("rising"), .Select("low")) register_19 (
    .D(_19), .en(En), .Q(\行19 ), .clk(CLK), .clr(RST));
  Register #(.width(32), .trigger("rising"), .Select("low")) register_20 (
    .D(_20), .en(En), .Q(\行20 ), .clk(CLK), .clr(RST));
  Register #(.width(32), .trigger("rising"), .Select("low")) register_21 (
    .D(_21), .en(En), .Q(\行21 ), .clk(CLK), .clr(RST));
  Register #(.width(32), .trigger("rising"), .Select("low")) register_22 (
    .D(_22), .en(En), .Q(\行22 ), .clk(CLK), .clr(RST));
  Register #(.width(32), .trigger("rising"), .Select("low")) register_23 (
    .D(_23), .en(En), .Q(\行23 ), .clk(CLK), .clr(RST));
  Register #(.width(32), .trigger("rising"), .Select("low")) register_24 (
    .D(_24), .en(En), .Q(\行24 ), .clk(CLK), .clr(RST));
  Register #(.width(32), .trigger("rising"), .Select("low")) register_25 (
    .D(_25), .en(En), .Q(\行25 ), .clk(CLK), .clr(RST));
  Register #(.width(32), .trigger("rising"), .Select("low")) register_26 (
    .D(_26), .en(En), .Q(\行26 ), .clk(CLK), .clr(RST));
  Register #(.width(32), .trigger("rising"), .Select("low")) register_27 (
    .D(_27), .en(En), .Q(\行27 ), .clk(CLK), .clr(RST));
  Register #(.width(32), .trigger("rising"), .Select("low")) register_28 (
    .D(_28), .en(En), .Q(\行28 ), .clk(CLK), .clr(RST));
  Register #(.width(32), .trigger("rising"), .Select("low")) register_29 (
    .D(_29), .en(En), .Q(\行29 ), .clk(CLK), .clr(RST));
  Register #(.width(32), .trigger("rising"), .Select("low")) register_30 (
    .D(_30), .en(En), .Q(\行30 ), .clk(CLK), .clr(RST));
  Register #(.width(32), .trigger("rising"), .Select("low")) register_31 (
    .D(_31), .en(En), .Q(\行31 ), .clk(CLK), .clr(RST));
  Register #(.width(32), .trigger("rising"), .Select("low")) register_32 (
    .D(_32), .en(En), .Q(\行32 ), .clk(CLK), .clr(RST));
endmodule

module H_16_toD_10 (
  input  [7:0] Hex_16,
  output [3:0] \百位 ,
  output [3:0] \十位 ,
  output [3:0] \个位 
);

  wire [7:0] divider_1_out, divider_1_rem, divider_2_out, divider_2_rem;

  Divider #(.width(8)) divider_1 (.a(Hex_16), .b(8'ha), .out(divider_1_out), .rem(divider_1_rem));  // open: upper
  Divider #(.width(8)) divider_2 (
    .a(divider_1_out), .b(8'ha), .out(divider_2_out), .rem(divider_2_rem));  // open: upper
  Bit_Extender #(.in_width(8), .out_width(4), .\type ("zero")) bit_extender_1 (.in(divider_2_out), .out(\百位 ));
  Bit_Extender #(.in_width(8), .out_width(4), .\type ("zero")) bit_extender_2 (.in(divider_2_rem), .out(\十位 ));
  Bit_Extender #(.in_width(8), .out_width(4), .\type ("zero")) bit_extender_3 (.in(divider_1_rem), .out(\个位 ));
endmodule

module GameOver (
  input  [7:0] delHP,
  input  [7:0] exHP,
  output [3:0] \百位 ,
  output [3:0] \十位 ,
  output [3:0] \个位 ,
  output Gameover
);

  wire comparator_1_eq, comparator_2_eq;
  wire [7:0] subtractor_1_out;

  Subtractor #(.width(8)) subtractor_1 (.a(exHP), .b(delHP), .out(subtractor_1_out));  // open: bin, bout
  H_16_toD_10 H_16_toD_10 (.Hex_16(subtractor_1_out), .\百位 (\百位 ), .\十位 (\十位 ), .\个位 (\个位 ));
  Comparator #(.width(4), .mode("twosComplement")) comparator_1 (
    .a(delHP[3:0]), .b(exHP[3:0]), .eq(comparator_1_eq));  // open: gt, lt
  Comparator #(.width(4), .mode("twosComplement")) comparator_2 (
    .a(delHP[7:4]), .b(exHP[7:4]), .eq(comparator_2_eq));  // open: gt, lt
  and and_1 (Gameover, comparator_1_eq, comparator_2_eq);
endmodule

module \频率控制电路  (
  input  [15:0] \延缓倍数 ,
  input  \原CLK ,
  input  RST,
  output \现CLK 
);

  wire comparator_1_eq, comparator_2_eq, comparator_2_gt, or_1_out;
  wire [15:0] counter_1_q, shifter_1_out;

  Counter #(.width(16), .max('hffff), .ongoal("wrap"), .trigger("rising"), .behavior("new")) counter_1 (
    .load(comparator_1_eq), .D({16{1'b0}}), .Q(counter_1_q), .clk(\原CLK ), .clr(RST));  // open: count, carry, preset, down
  Shifter #(.width(16), .shift("lr")) shifter_1 (.in(\延缓倍数 ), .\dist (4'b0001), .out(shifter_1_out));
  Comparator #(.width(16), .mode("twosComplement")) comparator_1 (
    .a(\延缓倍数 ), .b(counter_1_q), .eq(comparator_1_eq));  // open: gt, lt
  Comparator #(.width(16), .mode("twosComplement")) comparator_2 (
    .a(shifter_1_out), .b(counter_1_q), .gt(comparator_2_gt), .eq(comparator_2_eq));  // open: lt
  or or_1 (or_1_out, comparator_2_gt, comparator_2_eq);
  Multiplexer #(.select(1), .width(1), .disabled("Z"), .enable("false")) multiplexer_1 (
    .in0(1'b1), .in1(1'b0), .out(\现CLK ), .sel(or_1_out));
endmodule
